// Digital circuit Simplic-Refactor.dig as structural Verilog
module Simplic_Refactor (
  input  CLK,
  input  CLK_2
);

  wire add_4_c_o, add_6_c_o, add_7_c_o, add_8_c_o, add_9_c_o, and_1_out, and_2_out, and_4_out, and_5_out,
       and_6_out, and_7_out, and_8_out, and_10_out, and_11_out, and_12_out, and_13_out, and_14_out,
       and_15_out, and_16_out, and_17_out, and_19_out, C_3_q, C_4_q, C_5_q, C_6_q, C_q, comparator_1_eq,
       comparator_2_eq, multiplexer_3_out, multiplexer_8_out, multiplexer_9_out, multiplexer_10_out,
       multiplexer_11_out, N_3_q, N_4_q, N_5_q, N_6_q, N_q, nor_1_out, or_1_out, or_2_out, or_3_out,
       or_4_out, or_7_out, or_8_out, or_9_out, or_10_out, SEL_2_q, sub_1_c_o, sub_3_c_o, sub_4_c_o,
       sub_5_c_o, sub_6_c_o, undriven, undriven_17, undriven_18, undriven_25, undriven_63, undriven_88,
       undriven_91, undriven_93, undriven_95, undriven_103, undriven_104, undriven_121, undriven_153,
       undriven_154, undriven_155, undriven_157, undriven_158, undriven_159, undriven_160, undriven_161,
       undriven_162, undriven_163, undriven_167, undriven_173, undriven_174, undriven_175, undriven_176,
       undriven_177, undriven_178, undriven_179, undriven_180, undriven_181, undriven_182, undriven_183,
       undriven_184, undriven_185, undriven_186, undriven_187, undriven_188, undriven_189, undriven_190,
       undriven_191, V_3_q, V_4_q, V_5_q, V_6_q, V_q, xnor_1_out, xnor_2_out, xnor_3_out, xnor_4_out,
       xnor_5_out, xnor_6_out, xor_1_out, xor_2_out, xor_3_out, xor_4_out, xor_5_out, xor_6_out, xor_8_out,
       Z_3_q, Z_4_q, Z_5_q, Z_6_q, Z_q;
  wire [0:0] demultiplexer_5_out_0;
  wire [1:0] and_3_out, and_9_out, or_5_out, or_5_out_2, or_6_out, sub_2_c_o, undriven_192;
  wire [2:0] INSTR_2_d_2, INSTR_d_2;
  wire [3:0] C_2_q, not_1_out, not_2_out, undriven_58, undriven_59, undriven_60, undriven_118, undriven_119,
       undriven_120, undriven_164, undriven_165, undriven_166, undriven_194;
  wire [4:0] driver_17_out;
  wire [7:0] and_21_out, and_21_out_2, decoder_1_out_7, decoder_1_out_15, decoder_2_out_7, decoder_2_out_15,
       decoder_3_out_7, decoder_3_out_15, or_14_out, or_14_out_2;
  wire [11:0] INSTR_2_d, INSTR_d;
  wire [15:0] add_1_s, add_2_s, add_3_s, add_4_s, add_5_s, add_6_s, add_7_s, add_8_s, add_9_s, Addr_2_q,
       Addr_3_q, Addr_4_q, Addr_5_q, Addr_6_q, Addr_7_q, Addr_8_q, Addr_9_q, Addr_10_q, Addr_11_q, Addr_q,
       and_18_out, and_20_out, and_22_out, and_23_out, and_24_out, and_25_out, ASR_2_out, ASR_out,
       bitextender_1_out, bitextender_2_out, BUF_2_q, BUF_3_q, BUF_4_q, BUF_5_q, BUF_6_q, BUF_7_q, BUF_8_q,
       BUF_9_q, BUF_10_q, BUF_11_q, BUF_q, demultiplexer_1_out_0, demultiplexer_1_out_1,
       demultiplexer_1_out_2, demultiplexer_1_out_3, demultiplexer_1_out_4, demultiplexer_1_out_5,
       demultiplexer_1_out_6, demultiplexer_1_out_7, demultiplexer_1_out_8, demultiplexer_1_out_9,
       demultiplexer_1_out_10, demultiplexer_1_out_11, demultiplexer_1_out_12, demultiplexer_1_out_13,
       demultiplexer_1_out_14, demultiplexer_1_out_15, demultiplexer_2_out_0, demultiplexer_2_out_1,
       demultiplexer_2_out_2, demultiplexer_2_out_3, demultiplexer_2_out_4, demultiplexer_2_out_5,
       demultiplexer_2_out_6, demultiplexer_2_out_7, demultiplexer_2_out_8, demultiplexer_2_out_9,
       demultiplexer_2_out_10, demultiplexer_2_out_11, demultiplexer_2_out_12, demultiplexer_2_out_13,
       demultiplexer_2_out_14, demultiplexer_2_out_15, demultiplexer_3_out_0, demultiplexer_3_out_1,
       demultiplexer_3_out_2, demultiplexer_3_out_3, demultiplexer_3_out_4, demultiplexer_3_out_5,
       demultiplexer_3_out_6, demultiplexer_3_out_7, demultiplexer_3_out_8, demultiplexer_3_out_9,
       demultiplexer_3_out_10, demultiplexer_3_out_11, demultiplexer_3_out_12, demultiplexer_3_out_13,
       demultiplexer_3_out_14, demultiplexer_3_out_15, demultiplexer_4_out_0, demultiplexer_4_out_1,
       demultiplexer_4_out_2, demultiplexer_4_out_3, demultiplexer_4_out_4, demultiplexer_4_out_5,
       demultiplexer_4_out_6, demultiplexer_4_out_7, demultiplexer_4_out_8, demultiplexer_4_out_9,
       demultiplexer_4_out_10, demultiplexer_4_out_11, demultiplexer_4_out_12, demultiplexer_4_out_13,
       demultiplexer_4_out_14, demultiplexer_4_out_15, demultiplexer_5_out_1, demultiplexer_5_out_2,
       demultiplexer_5_out_3, demultiplexer_5_out_5, demultiplexer_5_out_6, demultiplexer_5_out_7,
       demultiplexer_5_out_9, demultiplexer_5_out_10, demultiplexer_5_out_11, demultiplexer_5_out_13,
       demultiplexer_5_out_14, demultiplexer_5_out_15, demultiplexer_6_out_0, demultiplexer_6_out_1,
       demultiplexer_6_out_2, demultiplexer_6_out_3, demultiplexer_6_out_4, demultiplexer_6_out_5,
       demultiplexer_6_out_6, demultiplexer_6_out_7, demultiplexer_6_out_8, demultiplexer_6_out_9,
       demultiplexer_6_out_10, demultiplexer_6_out_11, demultiplexer_6_out_12, demultiplexer_6_out_13,
       demultiplexer_6_out_14, demultiplexer_6_out_15, demultiplexer_7_out_0, demultiplexer_7_out_1,
       demultiplexer_7_out_2, demultiplexer_7_out_3, demultiplexer_7_out_4, demultiplexer_7_out_5,
       demultiplexer_7_out_6, demultiplexer_7_out_7, demultiplexer_7_out_8, demultiplexer_7_out_9,
       demultiplexer_7_out_10, demultiplexer_7_out_11, demultiplexer_7_out_12, demultiplexer_7_out_13,
       demultiplexer_7_out_14, demultiplexer_7_out_15, demultiplexer_8_out_0, demultiplexer_8_out_1,
       demultiplexer_8_out_2, demultiplexer_8_out_3, demultiplexer_8_out_4, demultiplexer_8_out_5,
       demultiplexer_8_out_6, demultiplexer_8_out_7, demultiplexer_8_out_8, demultiplexer_8_out_9,
       demultiplexer_8_out_10, demultiplexer_8_out_11, demultiplexer_8_out_12, demultiplexer_8_out_13,
       demultiplexer_8_out_14, demultiplexer_8_out_15, demultiplexer_9_out_0, demultiplexer_9_out_1,
       demultiplexer_9_out_2, demultiplexer_9_out_3, demultiplexer_9_out_4, demultiplexer_9_out_5,
       demultiplexer_9_out_6, demultiplexer_9_out_7, demultiplexer_9_out_8, demultiplexer_9_out_9,
       demultiplexer_9_out_10, demultiplexer_9_out_11, demultiplexer_9_out_12, demultiplexer_9_out_13,
       demultiplexer_9_out_14, demultiplexer_9_out_15, demultiplexer_10_out_0, demultiplexer_10_out_1,
       demultiplexer_10_out_2, demultiplexer_10_out_3, demultiplexer_10_out_4, demultiplexer_10_out_5,
       demultiplexer_10_out_6, demultiplexer_10_out_7, demultiplexer_10_out_8, demultiplexer_10_out_9,
       demultiplexer_10_out_10, demultiplexer_10_out_11, demultiplexer_10_out_12, demultiplexer_10_out_13,
       demultiplexer_10_out_14, demultiplexer_10_out_15, demultiplexer_11_out_0, demultiplexer_11_out_1,
       demultiplexer_11_out_2, demultiplexer_11_out_3, demultiplexer_11_out_4, demultiplexer_11_out_5,
       demultiplexer_11_out_6, demultiplexer_11_out_7, demultiplexer_11_out_8, demultiplexer_11_out_9,
       demultiplexer_11_out_10, demultiplexer_11_out_11, demultiplexer_11_out_12, demultiplexer_11_out_13,
       demultiplexer_11_out_14, demultiplexer_11_out_15, div_1_q, div_1_r, div_2_q, div_2_r, div_3_q,
       div_3_r, div_4_q, div_4_r, div_5_q, div_5_r, div_6_q, div_6_r, driver_1_out, driver_9_out, Link_2_q,
       Link_3_q, Link_4_q, Link_5_q, Link_6_q, Link_7_q, Link_8_q, Link_9_q, Link_10_q, Link_11_q, Link_q,
       LSL_2_out, LSL_3_out, LSL_out, LSR_2_out, LSR_out, MEM_2_d, MEM_d, mul_1_mul, mul_1_mul_2, mul_2_mul,
       mul_2_mul_2, mul_3_mul, mul_3_mul_2, mul_4_mul, mul_4_mul_2, mul_5_mul, mul_5_mul_2, mul_6_mul,
       mul_6_mul_2, multiplexer_5_out, multiplexer_6_out, multiplexer_7_out, multiplexer_12_out,
       multiplexer_13_out, multiplexer_14_out, multiplexer_15_out, multiplexer_16_out, multiplexer_17_out,
       multiplexer_18_out, multiplexer_19_out, multiplexer_20_out, multiplexer_21_out, multiplexer_22_out,
       multiplexer_23_out, multiplexer_24_out, multiplexer_25_out, multiplexer_26_out, multiplexer_27_out,
       multiplexer_28_out, multiplexer_29_out, multiplexer_30_out, multiplexer_31_out, multiplexer_32_out,
       multiplexer_33_out, multiplexer_34_out, multiplexer_35_out, multiplexer_36_out, multiplexer_37_out,
       multiplexer_38_out, multiplexer_39_out, multiplexer_40_out, multiplexer_42_out, multiplexer_44_out,
       multiplexer_45_out, multiplexer_46_out, multiplexer_47_out, multiplexer_48_out, multiplexer_49_out,
       multiplexer_50_out, multiplexer_51_out, multiplexer_52_out, multiplexer_54_out, multiplexer_55_out,
       multiplexer_56_out, multiplexer_57_out, multiplexer_58_out, multiplexer_59_out, multiplexer_60_out,
       multiplexer_61_out, multiplexer_62_out, nor_2_out, nor_3_out, nor_4_out, nor_5_out, nor_6_out,
       nor_7_out, or_11_out, or_12_out, or_13_out, or_15_out, or_16_out, or_17_out, or_18_out, PC_2_out,
       PC_3_out, PC_4_out, PC_5_out, PC_6_out, PC_7_out, PC_8_out, PC_9_out, PC_10_out, PC_11_out, PC_12_out,
       PC_out, R1_q, R2_q, R3_q, R4_q, R5_q, R6_q, R7_q, R8_q, R9_q, R91_q, R92_q, R93_q, R94_q, R95_q,
       R96_q, R97_q, R98_q, R99_q, R109_q, R110_q, R111_q, R112_q, R113_q, R114_q, R115_q, R116_q, R117_q,
       R118_q, R119_q, R120_q, R121_q, R122_q, R123_q, R124_q, R125_q, R126_q, R136_q, R137_q, R138_q,
       R139_q, R140_q, R141_q, R142_q, R143_q, R144_q, R145_q, R146_q, R147_q, R148_q, R149_q, R150_q,
       R151_q, R152_q, R153_q, R154_q, R155_q, R156_q, R157_q, R158_q, R159_q, R160_q, R161_q, R162_q,
       R172_q, R173_q, R174_q, R175_q, R176_q, R177_q, R178_q, R179_q, R180_q, R181_q, R182_q, R183_q,
       R184_q, R185_q, R186_q, R187_q, R188_q, R189_q, R190_q, R191_q, R192_q, R193_q, R194_q, R195_q,
       R196_q, R197_q, R198_q, R199_q, R200_q, R201_q, R202_q, R203_q, R204_q, R205_q, R206_q, R207_q,
       RET_2_q, RET_3_q, RET_4_q, RET_5_q, RET_6_q, RET_7_q, RET_8_q, RET_9_q, RET_10_q, RET_11_q, RET_q,
       ROR_2_out, ROR_out, STA_2_q, STA_3_q, STA_4_q, STA_5_q, STA_6_q, STA_7_q, STA_8_q, STA_9_q, STA_10_q,
       STA_11_q, STA_q, sub_1_s, sub_2_s, sub_3_s, sub_4_s, sub_5_s, sub_6_s, t29_q, t31_q, t33_q, t35_q,
       t36_q, t37_q, t38_q, t39_q, t40_q, t41_q, t42_q, undriven_16, undriven_19, undriven_20, undriven_21,
       undriven_22, undriven_23, undriven_24, undriven_26, undriven_27, undriven_28, undriven_29,
       undriven_31, undriven_32, undriven_33, undriven_34, undriven_46, undriven_51, undriven_52,
       undriven_53, undriven_54, undriven_55, undriven_56, undriven_57, undriven_61, undriven_62,
       undriven_65, undriven_66, undriven_67, undriven_68, undriven_69, undriven_70, undriven_71,
       undriven_72, undriven_73, undriven_74, undriven_75, undriven_76, undriven_77, undriven_79,
       undriven_80, undriven_97, undriven_98, undriven_99, undriven_100, undriven_101, undriven_102,
       undriven_105, undriven_106, undriven_107, undriven_108, undriven_109, undriven_110, undriven_111,
       undriven_112, undriven_113, undriven_114, undriven_115, undriven_116, undriven_117, undriven_150,
       undriven_151, undriven_152, undriven_156, undriven_168, undriven_169, undriven_170, undriven_171,
       undriven_172, undriven_193, undriven_195, undriven_196, undriven_197, xor_7_out, xor_9_out,
       xor_10_out, xor_11_out, xor_12_out, xor_13_out;
  wire [15:1] demultiplexer_5_out_0_2, demultiplexer_5_out_4, demultiplexer_5_out_8, demultiplexer_5_out_12,
       t30_q, t32_q, t34_q, undriven_30, undriven_35, undriven_36, undriven_37, undriven_38, undriven_39,
       undriven_40, undriven_41, undriven_42, undriven_43, undriven_44, undriven_45, undriven_47,
       undriven_48, undriven_49, undriven_50;
  wire [15:5] driver_17_out_2;
  wire [16:16] undriven_2, undriven_3, undriven_4, undriven_5, undriven_6, undriven_7, undriven_8,
       undriven_9, undriven_10, undriven_11, undriven_12, undriven_13, undriven_14, undriven_15, undriven_64,
       undriven_78, undriven_81, undriven_82, undriven_83, undriven_84, undriven_85, undriven_86,
       undriven_87, undriven_89, undriven_90, undriven_92, undriven_94, undriven_96, undriven_122,
       undriven_123, undriven_124, undriven_125, undriven_126, undriven_127, undriven_128, undriven_129,
       undriven_130, undriven_131, undriven_132, undriven_133, undriven_134, undriven_135, undriven_136,
       undriven_137, undriven_138, undriven_139, undriven_140, undriven_141, undriven_142, undriven_143,
       undriven_144, undriven_145, undriven_146, undriven_147, undriven_148, undriven_149;

  ROM #(.bigEndian("true"), .AddrBits(16), .Bits(16)) INSTR (
    .A(undriven_197), .sel(1'b1), .D({and_3_out[1], INSTR_d_2, INSTR_d}));
  EEPROMDualPort #(.AddrBits(16), .Bits(16)) MEM (
    .A(undriven_196), .Din(undriven_195), .str(and_1_out), .C(CLK_2), .ld(1'b1), .D(MEM_d));
  and and_1 (and_1_out, INSTR_d_2[0], INSTR_d_2[1], ~INSTR_d_2[2], ~and_3_out[1]);  // And
  and and_2 (and_2_out, INSTR_d_2[1], INSTR_d_2[2]);
  and and_3 (and_3_out[0], INSTR_d_2[0], ~and_3_out[1]);  // And
  or or_1 (or_1_out, and_2_out, and_3_out[1]);
  or or_2 (or_2_out, undriven_194[3], undriven_194[2]);
  or or_3 (or_3_out, ~undriven_194[3], undriven_194[2]);  // Or
  xor xor_1 (xor_1_out, undriven_194[3], undriven_194[0]);
  and and_4 (and_4_out, ~undriven_194[2], xnor_1_out);  // And
  or or_4 (or_4_out, undriven_194[2], ~xnor_1_out);  // Or
  xnor xnor_1 (xnor_1_out, undriven_194[3], undriven_194[0]);
  and and_5 (and_5_out, ~undriven_194[1], ~undriven_194[0]);  // And
  assign not_1_out = ~undriven_194;  // Not not_1, 4 bits wide
  ROM #(.bigEndian("true"), .AddrBits(16), .Bits(16)) INSTR_2 (
    .A(PC_3_out), .sel(1'b1), .D({and_9_out[1], INSTR_2_d_2, INSTR_2_d}));
  EEPROMDualPort #(.AddrBits(16), .Bits(16)) MEM_2 (
    .A(driver_9_out), .Din(driver_1_out), .str(and_6_out), .C(CLK), .ld(1'b1), .D(MEM_2_d));
  Multiplexer #(.Selector_Bits(4)) multiplexer_1 (
    .in_0(undriven_194[0]), .in_1(not_1_out[0]), .in_2(undriven_194[1]), .in_3(not_1_out[1]),
    .in_4(undriven_194[2]), .in_5(not_1_out[2]), .in_6(undriven_194[3]), .in_7(not_1_out[3]),
    .in_8(or_2_out), .in_9(or_3_out), .in_10(xor_1_out), .in_11(and_4_out), .in_12(or_4_out),
    .in_13(xnor_1_out), .in_14(and_5_out), .in_15(1'b1));  // open: sel, out
  assign {or_5_out_2, or_5_out} = INSTR_2_d[3:0] | INSTR_2_d[7:4] | INSTR_2_d[11:8];  // Or or_5, 4 bits wide
  and and_6 (and_6_out, INSTR_2_d_2[0], INSTR_2_d_2[1], ~INSTR_2_d_2[2], ~and_9_out[1]);  // And
  and and_7 (and_7_out, INSTR_2_d_2[1], ~INSTR_2_d_2[2], ~and_9_out[1]);  // And
  and and_8 (and_8_out, INSTR_2_d_2[1], INSTR_2_d_2[2]);
  and and_9 (and_9_out[0], INSTR_2_d_2[0], ~and_9_out[1]);  // And
  and and_10 (and_10_out, INSTR_2_d_2[0], INSTR_2_d_2[1], INSTR_2_d_2[2], and_9_out[1]);
  and and_11 (and_11_out, ~and_9_out[1], INSTR_2_d_2[2], INSTR_2_d_2[1], INSTR_2_d_2[0]);  // And
  assign or_6_out = or_5_out | or_5_out_2;  // Or or_6, 2 bits wide
  or or_7 (or_7_out, and_8_out, and_9_out[1]);
  and and_12 (and_12_out, nor_1_out, and_10_out);
  and and_13 (and_13_out, nor_1_out, and_11_out);
  nor nor_1 (nor_1_out, or_6_out[0], or_6_out[1]);
  BarrelShifter #(.Bits(16)) LSL (.in(undriven_193), .shift(undriven_191), .out(LSL_out));
  BarrelShifter #(.Bits(16), .direction("right")) LSR (.in(undriven_193), .shift(undriven_191), .out(LSR_out));
  BarrelShifter #(.Bits(16), .barrelShifterMode("arithmetic"), .direction("right")) ASR (
    .in(undriven_193), .shift(undriven_191), .out(ASR_out));
  BarrelShifter #(.Bits(16), .barrelShifterMode("rotate"), .direction("right")) ROR (
    .in(undriven_193), .shift(undriven_191), .out(ROR_out));
  or or_8 (or_8_out, C_2_q[3], C_2_q[2]);
  or or_9 (or_9_out, ~C_2_q[3], C_2_q[2]);  // Or
  xor xor_2 (xor_2_out, C_2_q[3], C_2_q[0]);
  and and_14 (and_14_out, ~C_2_q[2], xnor_2_out);  // And
  or or_10 (or_10_out, C_2_q[2], ~xnor_2_out);  // Or
  xnor xnor_2 (xnor_2_out, C_2_q[3], C_2_q[0]);
  and and_15 (and_15_out, ~C_2_q[1], ~C_2_q[0]);  // And
  Multiplexer #(.Selector_Bits(2), .Bits(16)) multiplexer_2 (
    .sel(undriven_192), .in_0(LSL_out), .in_1(LSR_out), .in_2(ASR_out), .in_3(ROR_out));  // open: out
  assign not_2_out = ~C_2_q;  // Not not_2, 4 bits wide
  Multiplexer #(.Selector_Bits(4)) multiplexer_3 (
    .sel(INSTR_2_d[3:0]), .in_0(C_2_q[0]), .in_1(not_2_out[0]), .in_2(C_2_q[1]), .in_3(not_2_out[1]),
    .in_4(C_2_q[2]), .in_5(not_2_out[2]), .in_6(C_2_q[3]), .in_7(not_2_out[3]), .in_8(or_8_out),
    .in_9(or_9_out), .in_10(xor_2_out), .in_11(and_14_out), .in_12(or_10_out), .in_13(xnor_2_out),
    .in_14(and_15_out), .in_15(1'b1), .out(multiplexer_3_out));
  Multiplexer #(.Selector_Bits(4)) multiplexer_4 (
    .in_0(undriven_176), .in_1(undriven_177), .in_2(undriven_178), .in_3(undriven_179), .in_4(undriven_180),
    .in_5(undriven_181), .in_6(undriven_182), .in_7(undriven_183), .in_8(undriven_184), .in_9(undriven_185),
    .in_10(undriven_186), .in_11(undriven_187), .in_12(undriven_188), .in_13(undriven_189),
    .in_14(undriven_190), .in_15(1'b1));  // open: sel, out
  Add #(.Bits(16)) add_1 (.a(driver_1_out), .b(16'h1), .c_i(1'b0), .s(add_1_s));  // open: c_o
  Add #(.Bits(16)) add_2 (.a(driver_1_out), .b(driver_9_out), .c_i(1'b0), .s(add_2_s));  // open: c_o
  BitExtender #(.inputBits(4)) bitextender_1 (.in(INSTR_2_d[3:0]), .out(bitextender_1_out));
  Multiplexer #(.Bits(16)) multiplexer_5 (
    .sel(multiplexer_3_out), .in_0(add_1_s), .in_1(driver_9_out), .out(multiplexer_5_out));
  Multiplexer #(.Bits(16)) multiplexer_6 (
    .sel(multiplexer_3_out), .in_0(add_1_s), .in_1(add_2_s), .out(multiplexer_6_out));
  Add #(.Bits(16)) add_3 (.a(driver_9_out), .b(bitextender_1_out), .c_i(1'b0), .s(add_3_s));  // open: c_o
  BarrelShifter #(.Bits(16)) LSL_2 (.in(driver_1_out), .shift(5'b01000), .out(LSL_2_out));
  assign or_11_out = {{8{1'b0}}, INSTR_2_d[7:0]} | LSL_2_out;  // Or or_11, 16 bits wide
  BarrelShifter #(.Bits(16)) LSL_3 (.in(driver_1_out), .shift(driver_17_out), .out(LSL_3_out));
  BarrelShifter #(.Bits(16), .direction("right")) LSR_2 (.in(driver_1_out), .shift(driver_17_out), .out(LSR_2_out));
  BarrelShifter #(.Bits(16), .barrelShifterMode("arithmetic"), .direction("right")) ASR_2 (
    .in(driver_1_out), .shift(driver_17_out), .out(ASR_2_out));
  BarrelShifter #(.Bits(16), .barrelShifterMode("rotate"), .direction("right")) ROR_2 (
    .in(driver_1_out), .shift(driver_17_out), .out(ROR_2_out));
  BitSelector #(.Selector_Bits(4)) bitselector_1 (.in(undriven_175), .sel(4'b1111));  // open: out
  BitSelector #(.Selector_Bits(4)) bitselector_2 (.in(undriven_174), .sel(4'b1111));  // open: out
  BitSelector #(.Selector_Bits(4)) bitselector_3 (.in(undriven_173), .sel(4'b1111));  // open: out
  Multiplexer #(.Selector_Bits(2), .Bits(16)) multiplexer_7 (
    .sel(INSTR_2_d[5:4]), .in_0(LSL_3_out), .in_1(LSR_2_out), .in_2(ASR_2_out), .in_3(ROR_2_out),
    .out(multiplexer_7_out));
  xnor xnor_3 (xnor_3_out, undriven_158, undriven_159);
  xor xor_3 (xor_3_out, undriven_160, undriven_161);
  xnor xnor_4 (xnor_4_out, undriven_162, undriven_163);
  Comparator #(.Bits(16)) comparator_1 (.a(multiplexer_13_out), .b({16{1'b0}}), .eq(comparator_1_eq));  // open: gt, lt
  Comparator #(.Bits(16)) comparator_2 (.a(undriven_156), .b({16{1'b0}}), .eq(comparator_2_eq));  // open: gt, lt
  xnor xnor_5 (xnor_5_out, driver_9_out[15], driver_17_out_2[15]);
  xor xor_4 (xor_4_out, driver_9_out[15], driver_17_out_2[15]);
  xnor xnor_6 (xnor_6_out, driver_17_out_2[15], multiplexer_13_out[15]);
  xor xor_5 (xor_5_out, xnor_3_out, undriven_155);
  and and_16 (and_16_out, xor_3_out, xnor_4_out);
  xor xor_6 (xor_6_out, xnor_5_out, multiplexer_13_out[15]);
  and and_17 (and_17_out, xor_4_out, xnor_6_out);
  Multiplexer multiplexer_8 (.sel(undriven_167), .in_0(add_4_c_o), .in_1(sub_1_c_o), .out(multiplexer_8_out));
  Multiplexer multiplexer_9 (.sel(undriven_167), .in_0(xor_5_out), .in_1(and_16_out), .out(multiplexer_9_out));
  Multiplexer #(.Selector_Bits(2)) multiplexer_10 (
    .sel(and_9_out), .in_0(xor_6_out), .in_1(and_17_out), .in_2(1'b0), .in_3(1'b0), .out(multiplexer_10_out));
  Register SEL (.C(undriven_153));  // open: D, en, Q
  Register Z (.D(comparator_2_eq), .C(undriven_153), .en(undriven_154), .Q(Z_q));
  Register N (.D(undriven_157), .C(undriven_153), .en(undriven_154), .Q(N_q));
  Register C (.D(multiplexer_8_out), .C(undriven_153), .en(undriven_154), .Q(C_q));
  Register V (.D(multiplexer_9_out), .C(undriven_153), .en(undriven_154), .Q(V_q));
  Multiplexer #(.Selector_Bits(2)) multiplexer_11 (
    .sel(and_9_out), .in_0(sub_2_c_o[1]), .in_1(sub_2_c_o[0]), .in_2(1'b0), .in_3(1'b0),
    .out(multiplexer_11_out));
  Add #(.Bits(16)) add_4 (.a(undriven_152), .b(undriven_151), .c_i(C_q), .s(add_4_s), .c_o(add_4_c_o));
  Sub #(.Bits(16)) sub_1 (.a(undriven_152), .b(undriven_151), .c_i(C_q), .s(sub_1_s), .c_o(sub_1_c_o));
  Mul #(.Bits(16)) mul_1 (.a(undriven_152), .b(undriven_151), .mul({mul_1_mul_2, mul_1_mul}));
  Div #(.Bits(16)) div_1 (.a(undriven_152), .b(undriven_151), .q(div_1_q), .r(div_1_r));
  assign and_18_out = undriven_152 & undriven_151;  // And and_18, 16 bits wide
  assign or_12_out = undriven_152 | undriven_151;  // Or or_12, 16 bits wide
  assign xor_7_out = undriven_152 ^ undriven_151;  // XOr xor_7, 16 bits wide
  assign nor_2_out = ~(undriven_152 | undriven_151);  // NOr nor_2, 16 bits wide
  xor xor_8 (xor_8_out, and_12_out, and_13_out);
  Register SEL_2 (.D(and_12_out), .C(CLK), .en(xor_8_out), .Q(SEL_2_q));
  and and_19 (and_19_out, SEL_2_q, or_7_out);
  Register N_2 (.D(multiplexer_13_out[15]), .C(CLK), .en(and_19_out), .Q(C_2_q[3]));
  Register Z_2 (.D(comparator_1_eq), .C(CLK), .en(and_19_out), .Q(C_2_q[2]));
  Register C_2 (.D(multiplexer_11_out), .C(CLK), .en(and_19_out), .Q(C_2_q[1]));
  Register V_2 (.D(multiplexer_10_out), .C(CLK), .en(and_19_out), .Q(C_2_q[0]));
  Multiplexer #(.Selector_Bits(4), .Bits(16)) multiplexer_12 (
    .in_0(undriven_168), .in_1(undriven_169), .in_2(undriven_170), .in_3(multiplexer_26_out),
    .in_4(undriven_171), .in_5(undriven_172), .in_6(add_4_s), .in_7(sub_1_s), .in_8(mul_1_mul),
    .in_9(mul_1_mul_2), .in_10(div_1_q), .in_11(div_1_r), .in_12(and_18_out), .in_13(or_12_out),
    .in_14(xor_7_out), .in_15(nor_2_out), .out(multiplexer_12_out));  // open: sel
  Demultiplexer #(.Selector_Bits(4), .Bits(16)) demultiplexer_1 (
    .in(undriven_150), .out_0(demultiplexer_1_out_0), .out_1(demultiplexer_1_out_1),
    .out_2(demultiplexer_1_out_2), .out_3(demultiplexer_1_out_3), .out_4(demultiplexer_1_out_4),
    .out_5(demultiplexer_1_out_5), .out_6(demultiplexer_1_out_6), .out_7(demultiplexer_1_out_7),
    .out_8(demultiplexer_1_out_8), .out_9(demultiplexer_1_out_9), .out_10(demultiplexer_1_out_10),
    .out_11(demultiplexer_1_out_11), .out_12(demultiplexer_1_out_12), .out_13(demultiplexer_1_out_13),
    .out_14(demultiplexer_1_out_14), .out_15(demultiplexer_1_out_15));  // open: sel
  Demultiplexer #(.Selector_Bits(4), .Bits(16)) demultiplexer_2 (
    .sel(undriven_164), .in(multiplexer_12_out), .out_0(demultiplexer_2_out_0),
    .out_1(demultiplexer_2_out_1), .out_2(demultiplexer_2_out_2), .out_3(demultiplexer_2_out_3),
    .out_4(demultiplexer_2_out_4), .out_5(demultiplexer_2_out_5), .out_6(demultiplexer_2_out_6),
    .out_7(demultiplexer_2_out_7), .out_8(demultiplexer_2_out_8), .out_9(demultiplexer_2_out_9),
    .out_10(demultiplexer_2_out_10), .out_11(demultiplexer_2_out_11), .out_12(demultiplexer_2_out_12),
    .out_13(demultiplexer_2_out_13), .out_14(demultiplexer_2_out_14), .out_15(demultiplexer_2_out_15));
  Add #(.Bits(16)) add_5 (
    .a(driver_9_out), .b({driver_17_out_2, driver_17_out}), .c_i(C_2_q[1]), .s(add_5_s), .c_o(sub_2_c_o[1]));
  Sub #(.Bits(16)) sub_2 (
    .a(driver_9_out), .b({driver_17_out_2, driver_17_out}), .c_i(C_2_q[1]), .s(sub_2_s), .c_o(sub_2_c_o[0]));
  Mul #(.Bits(16)) mul_2 (.a(driver_9_out), .b({driver_17_out_2, driver_17_out}), .mul({mul_2_mul_2, mul_2_mul}));
  Div #(.Bits(16)) div_2 (.a(driver_9_out), .b({driver_17_out_2, driver_17_out}), .q(div_2_q), .r(div_2_r));
  assign and_20_out = driver_9_out & {driver_17_out_2, driver_17_out};  // And and_20, 16 bits wide
  assign or_13_out = driver_9_out | {driver_17_out_2, driver_17_out};  // Or or_13, 16 bits wide
  assign xor_9_out = driver_9_out ^ {driver_17_out_2, driver_17_out};  // XOr xor_9, 16 bits wide
  assign nor_3_out = ~(driver_9_out | {driver_17_out_2, driver_17_out});  // NOr nor_3, 16 bits wide
  Register #(.Bits(16)) R200 (.D(demultiplexer_1_out_2), .C(undriven_121), .en(undriven_148[16]), .Q(R200_q));
  Register #(.Bits(16)) R202 (.D(demultiplexer_1_out_4), .C(undriven_121), .en(undriven_146[16]), .Q(R202_q));
  Register #(.Bits(16)) R204 (.D(demultiplexer_1_out_6), .C(undriven_121), .en(undriven_142[16]), .Q(R204_q));
  Register #(.Bits(16)) R206 (.D(demultiplexer_1_out_8), .C(undriven_121), .en(undriven_138[16]), .Q(R206_q));
  Register #(.Bits(16)) BUF (.D(demultiplexer_1_out_10), .C(undriven_121), .en(undriven_134[16]), .Q(BUF_q));
  Register #(.Bits(16)) STA (.D(demultiplexer_1_out_12), .C(undriven_121), .en(undriven_130[16]), .Q(STA_q));
  Register #(.Bits(16)) Link (.D(demultiplexer_1_out_14), .C(undriven_121), .en(undriven_126[16]), .Q(Link_q));
  Register #(.Bits(16)) R2 (.D(demultiplexer_2_out_2), .C(undriven_153), .en(undriven_143[16]), .Q(R2_q));
  Register #(.Bits(16)) R4 (.D(demultiplexer_2_out_4), .C(undriven_153), .en(undriven_139[16]), .Q(R4_q));
  Register #(.Bits(16)) R6 (.D(demultiplexer_2_out_6), .C(undriven_153), .en(undriven_135[16]), .Q(R6_q));
  Register #(.Bits(16)) R8 (.D(demultiplexer_2_out_8), .C(undriven_153), .en(undriven_131[16]), .Q(R8_q));
  Register #(.Bits(16)) BUF_2 (.D(demultiplexer_2_out_10), .C(undriven_153), .en(undriven_127[16]), .Q(BUF_2_q));
  Register #(.Bits(16)) STA_2 (.D(demultiplexer_2_out_12), .C(undriven_153), .en(undriven_124[16]), .Q(STA_2_q));
  Register #(.Bits(16)) Link_2 (.D(demultiplexer_2_out_14), .C(undriven_153), .en(undriven_122[16]), .Q(Link_2_q));
  BitExtender #(.inputBits(1)) bitextender_2 (.in(and_7_out), .out(bitextender_2_out));
  Register #(.Bits(16)) R1 (.D(demultiplexer_2_out_1), .C(undriven_153), .en(undriven_145[16]), .Q(R1_q));
  Register #(.Bits(16)) R3 (.D(demultiplexer_2_out_3), .C(undriven_153), .en(undriven_141[16]), .Q(R3_q));
  Register #(.Bits(16)) R5 (.D(demultiplexer_2_out_5), .C(undriven_153), .en(undriven_137[16]), .Q(R5_q));
  Register #(.Bits(16)) R7 (.D(demultiplexer_2_out_7), .C(undriven_153), .en(undriven_133[16]), .Q(R7_q));
  Register #(.Bits(16)) R9 (.D(demultiplexer_2_out_9), .C(undriven_153), .en(undriven_129[16]), .Q(R9_q));
  Register #(.Bits(16)) RET (.D(demultiplexer_2_out_11), .C(undriven_153), .en(undriven_125[16]), .Q(RET_q));
  Register #(.Bits(16)) Addr (.D(demultiplexer_2_out_13), .C(undriven_153), .en(undriven_123[16]), .Q(Addr_q));
  CounterPreset #(.Bits(16)) PC (
    .en(1'b1), .C(undriven_153), .dir(1'b0), .in(demultiplexer_2_out_15), .out(PC_out));  // open: ld, clr, ovf
  Register #(.Bits(16)) R199 (.D(demultiplexer_1_out_1), .C(undriven_121), .en(undriven_149[16]), .Q(R199_q));
  Register #(.Bits(16)) R201 (.D(demultiplexer_1_out_3), .C(undriven_121), .en(undriven_147[16]), .Q(R201_q));
  Register #(.Bits(16)) R203 (.D(demultiplexer_1_out_5), .C(undriven_121), .en(undriven_144[16]), .Q(R203_q));
  Register #(.Bits(16)) R205 (.D(demultiplexer_1_out_7), .C(undriven_121), .en(undriven_140[16]), .Q(R205_q));
  Register #(.Bits(16)) R207 (.D(demultiplexer_1_out_9), .C(undriven_121), .en(undriven_136[16]), .Q(R207_q));
  Register #(.Bits(16)) RET_2 (.D(demultiplexer_1_out_11), .C(undriven_121), .en(undriven_132[16]), .Q(RET_2_q));
  Register #(.Bits(16)) Addr_2 (.D(demultiplexer_1_out_13), .C(undriven_121), .en(undriven_128[16]), .Q(Addr_2_q));
  CounterPreset #(.Bits(16)) PC_2 (
    .en(1'b1), .C(undriven_121), .dir(1'b0), .in(demultiplexer_1_out_15), .out(PC_2_out));  // open: ld, clr, ovf
  Multiplexer #(.Selector_Bits(4), .Bits(16)) multiplexer_13 (
    .sel({and_9_out[1], INSTR_2_d_2}), .in_0(multiplexer_5_out), .in_1(multiplexer_6_out), .in_2(MEM_2_d),
    .in_3(driver_1_out), .in_4(or_11_out), .in_5(multiplexer_7_out), .in_6(add_5_s), .in_7(sub_2_s),
    .in_8(mul_2_mul), .in_9(mul_2_mul_2), .in_10(div_2_q), .in_11(div_2_r), .in_12(and_20_out),
    .in_13(or_13_out), .in_14(xor_9_out), .in_15(nor_3_out), .out(multiplexer_13_out));
  Decoder #(.Selector_Bits(4)) decoder_1 (
    .sel(INSTR_2_d[3:0]), .out_0(decoder_1_out_7[0]), .out_1(decoder_1_out_7[1]), .out_2(decoder_1_out_7[2]),
    .out_3(decoder_1_out_7[3]), .out_4(decoder_1_out_7[4]), .out_5(decoder_1_out_7[5]),
    .out_6(decoder_1_out_7[6]), .out_7(decoder_1_out_7[7]), .out_8(decoder_1_out_15[0]),
    .out_9(decoder_1_out_15[1]), .out_10(decoder_1_out_15[2]), .out_11(decoder_1_out_15[3]),
    .out_12(decoder_1_out_15[4]), .out_13(decoder_1_out_15[5]), .out_14(decoder_1_out_15[6]),
    .out_15(decoder_1_out_15[7]));
  Decoder #(.Selector_Bits(4)) decoder_2 (
    .sel(INSTR_2_d[7:4]), .out_0(decoder_2_out_7[0]), .out_1(decoder_2_out_7[1]), .out_2(decoder_2_out_7[2]),
    .out_3(decoder_2_out_7[3]), .out_4(decoder_2_out_7[4]), .out_5(decoder_2_out_7[5]),
    .out_6(decoder_2_out_7[6]), .out_7(decoder_2_out_7[7]), .out_8(decoder_2_out_15[0]),
    .out_9(decoder_2_out_15[1]), .out_10(decoder_2_out_15[2]), .out_11(decoder_2_out_15[3]),
    .out_12(decoder_2_out_15[4]), .out_13(decoder_2_out_15[5]), .out_14(decoder_2_out_15[6]),
    .out_15(decoder_2_out_15[7]));
  Decoder #(.Selector_Bits(4)) decoder_3 (
    .sel(INSTR_2_d[11:8]), .out_0(decoder_3_out_7[0]), .out_1(decoder_3_out_7[1]),
    .out_2(decoder_3_out_7[2]), .out_3(decoder_3_out_7[3]), .out_4(decoder_3_out_7[4]),
    .out_5(decoder_3_out_7[5]), .out_6(decoder_3_out_7[6]), .out_7(decoder_3_out_7[7]),
    .out_8(decoder_3_out_15[0]), .out_9(decoder_3_out_15[1]), .out_10(decoder_3_out_15[2]),
    .out_11(decoder_3_out_15[3]), .out_12(decoder_3_out_15[4]), .out_13(decoder_3_out_15[5]),
    .out_14(decoder_3_out_15[6]), .out_15(decoder_3_out_15[7]));
  assign {or_14_out_2, or_14_out} = {and_21_out_2, and_21_out} | {decoder_3_out_15, decoder_3_out_7};  // Or or_14, 16 bits wide
  assign {and_21_out_2, and_21_out} = bitextender_2_out & {decoder_2_out_15, decoder_2_out_7};  // And and_21, 16 bits wide
  Multiplexer #(.Bits(16)) multiplexer_14 (
    .sel(and_21_out[1]), .in_0(multiplexer_13_out), .in_1(add_3_s), .out(multiplexer_14_out));
  Multiplexer #(.Bits(16)) multiplexer_15 (
    .sel(and_21_out[2]), .in_0(multiplexer_13_out), .in_1(add_3_s), .out(multiplexer_15_out));
  Multiplexer #(.Bits(16)) multiplexer_16 (
    .sel(and_21_out[3]), .in_0(multiplexer_13_out), .in_1(add_3_s), .out(multiplexer_16_out));
  Multiplexer #(.Bits(16)) multiplexer_17 (
    .sel(and_21_out[4]), .in_0(multiplexer_13_out), .in_1(add_3_s), .out(multiplexer_17_out));
  Multiplexer #(.Bits(16)) multiplexer_18 (
    .sel(and_21_out[5]), .in_0(multiplexer_13_out), .in_1(add_3_s), .out(multiplexer_18_out));
  Multiplexer #(.Bits(16)) multiplexer_19 (
    .sel(and_21_out[6]), .in_0(multiplexer_13_out), .in_1(add_3_s), .out(multiplexer_19_out));
  Multiplexer #(.Bits(16)) multiplexer_20 (
    .sel(and_21_out[7]), .in_0(multiplexer_13_out), .in_1(add_3_s), .out(multiplexer_20_out));
  Multiplexer #(.Selector_Bits(4), .Bits(16)) multiplexer_21 (
    .sel(undriven_120), .in_0({16{1'b0}}), .in_1(R199_q), .in_2(R200_q), .in_3(R201_q), .in_4(R202_q),
    .in_5(R203_q), .in_6(R204_q), .in_7(R205_q), .in_8(R206_q), .in_9(R207_q), .in_10(BUF_q),
    .in_11(RET_2_q), .in_12(STA_q), .in_13(Addr_2_q), .in_14(Link_q), .in_15(PC_2_out),
    .out(multiplexer_21_out));
  Multiplexer #(.Selector_Bits(4), .Bits(16)) multiplexer_22 (
    .sel(undriven_119), .in_0({16{1'b0}}), .in_1(R199_q), .in_2(R200_q), .in_3(R201_q), .in_4(R202_q),
    .in_5(R203_q), .in_6(R204_q), .in_7(R205_q), .in_8(R206_q), .in_9(R207_q), .in_10(BUF_q),
    .in_11(RET_2_q), .in_12(STA_q), .in_13(Addr_2_q), .in_14(Link_q), .in_15(PC_2_out),
    .out(multiplexer_22_out));
  Multiplexer #(.Selector_Bits(4), .Bits(16)) multiplexer_23 (
    .sel(undriven_118), .in_0({16{1'b0}}), .in_1(R199_q), .in_2(R200_q), .in_3(R201_q), .in_4(R202_q),
    .in_5(R203_q), .in_6(R204_q), .in_7(R205_q), .in_8(R206_q), .in_9(R207_q), .in_10(BUF_q),
    .in_11(RET_2_q), .in_12(STA_q), .in_13(Addr_2_q), .in_14(Link_q), .in_15(PC_2_out),
    .out(multiplexer_23_out));
  Register #(.Bits(16)) R136 (.D(multiplexer_14_out), .C(CLK), .en(or_14_out[1]), .Q(R136_q));
  Register #(.Bits(16)) R137 (.D(multiplexer_15_out), .C(CLK), .en(or_14_out[2]), .Q(R137_q));
  Register #(.Bits(16)) R138 (.D(multiplexer_16_out), .C(CLK), .en(or_14_out[3]), .Q(R138_q));
  Register #(.Bits(16)) R139 (.D(multiplexer_17_out), .C(CLK), .en(or_14_out[4]), .Q(R139_q));
  Register #(.Bits(16)) R140 (.D(multiplexer_18_out), .C(CLK), .en(or_14_out[5]), .Q(R140_q));
  Register #(.Bits(16)) R141 (.D(multiplexer_19_out), .C(CLK), .en(or_14_out[6]), .Q(R141_q));
  Register #(.Bits(16)) R142 (.D(multiplexer_20_out), .C(CLK), .en(or_14_out[7]), .Q(R142_q));
  Multiplexer #(.Selector_Bits(4), .Bits(16)) multiplexer_24 (
    .sel(undriven_166), .in_0({16{1'b0}}), .in_1(R1_q), .in_2(R2_q), .in_3(R3_q), .in_4(R4_q), .in_5(R5_q),
    .in_6(R6_q), .in_7(R7_q), .in_8(R8_q), .in_9(R9_q), .in_10(BUF_2_q), .in_11(RET_q), .in_12(STA_2_q),
    .in_13(Addr_q), .in_14(Link_2_q), .in_15(PC_out), .out(multiplexer_24_out));
  Multiplexer #(.Selector_Bits(4), .Bits(16)) multiplexer_25 (
    .sel(undriven_165), .in_0({16{1'b0}}), .in_1(R1_q), .in_2(R2_q), .in_3(R3_q), .in_4(R4_q), .in_5(R5_q),
    .in_6(R6_q), .in_7(R7_q), .in_8(R8_q), .in_9(R9_q), .in_10(BUF_2_q), .in_11(RET_q), .in_12(STA_2_q),
    .in_13(Addr_q), .in_14(Link_2_q), .in_15(PC_out), .out(multiplexer_25_out));
  Multiplexer #(.Selector_Bits(4), .Bits(16)) multiplexer_26 (
    .sel(undriven_164), .in_0({16{1'b0}}), .in_1(R1_q), .in_2(R2_q), .in_3(R3_q), .in_4(R4_q), .in_5(R5_q),
    .in_6(R6_q), .in_7(R7_q), .in_8(R8_q), .in_9(R9_q), .in_10(BUF_2_q), .in_11(RET_q), .in_12(STA_2_q),
    .in_13(Addr_q), .in_14(Link_2_q), .in_15(PC_out), .out(multiplexer_26_out));
  assign driver_1_out = decoder_3_out_7[0] ? {16{1'b0}} : 16'bz;  // Driver driver_1
  assign driver_1_out = decoder_3_out_7[1] ? R136_q : 16'bz;  // Driver driver_2
  assign driver_1_out = decoder_3_out_7[2] ? R137_q : 16'bz;  // Driver driver_3
  assign driver_1_out = decoder_3_out_7[3] ? R138_q : 16'bz;  // Driver driver_4
  assign driver_1_out = decoder_3_out_7[4] ? R139_q : 16'bz;  // Driver driver_5
  assign driver_1_out = decoder_3_out_7[5] ? R140_q : 16'bz;  // Driver driver_6
  assign driver_1_out = decoder_3_out_7[6] ? R141_q : 16'bz;  // Driver driver_7
  assign driver_1_out = decoder_3_out_7[7] ? R142_q : 16'bz;  // Driver driver_8
  assign driver_9_out = decoder_2_out_7[0] ? {16{1'b0}} : 16'bz;  // Driver driver_9
  assign driver_9_out = decoder_2_out_7[1] ? R136_q : 16'bz;  // Driver driver_10
  assign driver_9_out = decoder_2_out_7[2] ? R137_q : 16'bz;  // Driver driver_11
  assign driver_9_out = decoder_2_out_7[3] ? R138_q : 16'bz;  // Driver driver_12
  assign driver_9_out = decoder_2_out_7[4] ? R139_q : 16'bz;  // Driver driver_13
  assign driver_9_out = decoder_2_out_7[5] ? R140_q : 16'bz;  // Driver driver_14
  assign driver_9_out = decoder_2_out_7[6] ? R141_q : 16'bz;  // Driver driver_15
  assign driver_9_out = decoder_2_out_7[7] ? R142_q : 16'bz;  // Driver driver_16
  assign {driver_17_out_2, driver_17_out} = decoder_1_out_7[0] ? {16{1'b0}} : 16'bz;  // Driver driver_17
  // Probe on R136_q
  assign {driver_17_out_2, driver_17_out} = decoder_1_out_7[1] ? R136_q : 16'bz;  // Driver driver_18
  // Probe on R137_q
  assign {driver_17_out_2, driver_17_out} = decoder_1_out_7[2] ? R137_q : 16'bz;  // Driver driver_19
  // Probe on R138_q
  assign {driver_17_out_2, driver_17_out} = decoder_1_out_7[3] ? R138_q : 16'bz;  // Driver driver_20
  // Probe on R139_q
  assign {driver_17_out_2, driver_17_out} = decoder_1_out_7[4] ? R139_q : 16'bz;  // Driver driver_21
  // Probe on R140_q
  assign {driver_17_out_2, driver_17_out} = decoder_1_out_7[5] ? R140_q : 16'bz;  // Driver driver_22
  // Probe on R141_q
  assign {driver_17_out_2, driver_17_out} = decoder_1_out_7[6] ? R141_q : 16'bz;  // Driver driver_23
  // Probe on R142_q
  assign {driver_17_out_2, driver_17_out} = decoder_1_out_7[7] ? R142_q : 16'bz;  // Driver driver_24
  Multiplexer #(.Bits(16)) multiplexer_27 (
    .sel(and_21_out_2[0]), .in_0(multiplexer_13_out), .in_1(add_3_s), .out(multiplexer_27_out));
  Multiplexer #(.Bits(16)) multiplexer_28 (
    .sel(and_21_out_2[1]), .in_0(multiplexer_13_out), .in_1(add_3_s), .out(multiplexer_28_out));
  Multiplexer #(.Bits(16)) multiplexer_29 (
    .sel(and_21_out_2[2]), .in_0(multiplexer_13_out), .in_1(add_3_s), .out(multiplexer_29_out));
  Multiplexer #(.Bits(16)) multiplexer_30 (
    .sel(and_21_out_2[3]), .in_0(multiplexer_13_out), .in_1(add_3_s), .out(multiplexer_30_out));
  Multiplexer #(.Bits(16)) multiplexer_31 (
    .sel(and_21_out_2[4]), .in_0(multiplexer_13_out), .in_1(add_3_s), .out(multiplexer_31_out));
  Multiplexer #(.Bits(16)) multiplexer_32 (
    .sel(and_21_out_2[5]), .in_0(multiplexer_13_out), .in_1(add_3_s), .out(multiplexer_32_out));
  Multiplexer #(.Bits(16)) multiplexer_33 (
    .sel(and_21_out_2[6]), .in_0(multiplexer_13_out), .in_1(add_3_s), .out(multiplexer_33_out));
  Multiplexer #(.Bits(16)) multiplexer_34 (
    .sel(and_21_out_2[7]), .in_0(multiplexer_13_out), .in_1(add_3_s), .out(multiplexer_34_out));
  Register #(.Bits(16)) R143 (.D(multiplexer_27_out), .C(CLK), .en(or_14_out_2[0]), .Q(R143_q));
  Register #(.Bits(16)) R144 (.D(multiplexer_28_out), .C(CLK), .en(or_14_out_2[1]), .Q(R144_q));
  Register #(.Bits(16)) BUF_3 (.D(multiplexer_29_out), .C(CLK), .en(or_14_out_2[2]), .Q(BUF_3_q));
  Register #(.Bits(16)) RET_3 (.D(multiplexer_30_out), .C(CLK), .en(or_14_out_2[3]), .Q(RET_3_q));
  Register #(.Bits(16)) STA_3 (.D(multiplexer_31_out), .C(CLK), .en(or_14_out_2[4]), .Q(STA_3_q));
  Register #(.Bits(16)) Addr_3 (.D(multiplexer_32_out), .C(CLK), .en(or_14_out_2[5]), .Q(Addr_3_q));
  Register #(.Bits(16)) Link_3 (.D(multiplexer_33_out), .C(CLK), .en(or_14_out_2[6]), .Q(Link_3_q));
  CounterPreset #(.Bits(16)) PC_3 (
    .en(1'b1), .C(CLK), .dir(1'b0), .in(multiplexer_34_out), .ld(or_14_out_2[7]), .clr(1'b0), .out(PC_3_out));  // open: ovf
  assign driver_1_out = decoder_3_out_15[0] ? R143_q : 16'bz;  // Driver driver_25
  assign driver_1_out = decoder_3_out_15[1] ? R144_q : 16'bz;  // Driver driver_26
  assign driver_1_out = decoder_3_out_15[2] ? BUF_3_q : 16'bz;  // Driver driver_27
  assign driver_1_out = decoder_3_out_15[3] ? RET_3_q : 16'bz;  // Driver driver_28
  assign driver_1_out = decoder_3_out_15[4] ? STA_3_q : 16'bz;  // Driver driver_29
  assign driver_1_out = decoder_3_out_15[5] ? Addr_3_q : 16'bz;  // Driver driver_30
  assign driver_1_out = decoder_3_out_15[6] ? Link_3_q : 16'bz;  // Driver driver_31
  assign driver_1_out = decoder_3_out_15[7] ? PC_3_out : 16'bz;  // Driver driver_32
  assign driver_9_out = decoder_2_out_15[0] ? R143_q : 16'bz;  // Driver driver_33
  assign driver_9_out = decoder_2_out_15[1] ? R144_q : 16'bz;  // Driver driver_34
  assign driver_9_out = decoder_2_out_15[2] ? BUF_3_q : 16'bz;  // Driver driver_35
  assign driver_9_out = decoder_2_out_15[3] ? RET_3_q : 16'bz;  // Driver driver_36
  assign driver_9_out = decoder_2_out_15[4] ? STA_3_q : 16'bz;  // Driver driver_37
  assign driver_9_out = decoder_2_out_15[5] ? Addr_3_q : 16'bz;  // Driver driver_38
  assign driver_9_out = decoder_2_out_15[6] ? Link_3_q : 16'bz;  // Driver driver_39
  assign driver_9_out = decoder_2_out_15[7] ? PC_3_out : 16'bz;  // Driver driver_40
  assign {driver_17_out_2, driver_17_out} = decoder_1_out_15[0] ? R143_q : 16'bz;  // Driver driver_41
  assign {driver_17_out_2, driver_17_out} = decoder_1_out_15[1] ? R144_q : 16'bz;  // Driver driver_42
  assign {driver_17_out_2, driver_17_out} = decoder_1_out_15[2] ? BUF_3_q : 16'bz;  // Driver driver_43
  assign {driver_17_out_2, driver_17_out} = decoder_1_out_15[3] ? RET_3_q : 16'bz;  // Driver driver_44
  assign {driver_17_out_2, driver_17_out} = decoder_1_out_15[4] ? STA_3_q : 16'bz;  // Driver driver_45
  assign {driver_17_out_2, driver_17_out} = decoder_1_out_15[5] ? Addr_3_q : 16'bz;  // Driver driver_46
  assign {driver_17_out_2, driver_17_out} = decoder_1_out_15[6] ? Link_3_q : 16'bz;  // Driver driver_47
  assign {driver_17_out_2, driver_17_out} = decoder_1_out_15[7] ? PC_3_out : 16'bz;  // Driver driver_48
  // Probe on R143_q
  // Probe on R144_q
  // Probe on BUF_3_q
  // Probe on RET_3_q
  // Probe on STA_3_q
  // Probe on Addr_3_q
  // Probe on Link_3_q
  // Probe on PC_3_out
  Demultiplexer #(.Selector_Bits(4), .Bits(16)) demultiplexer_3 (
    .out_0(demultiplexer_3_out_0), .out_1(demultiplexer_3_out_1), .out_2(demultiplexer_3_out_2),
    .out_3(demultiplexer_3_out_3), .out_4(demultiplexer_3_out_4), .out_5(demultiplexer_3_out_5),
    .out_6(demultiplexer_3_out_6), .out_7(demultiplexer_3_out_7), .out_8(demultiplexer_3_out_8),
    .out_9(demultiplexer_3_out_9), .out_10(demultiplexer_3_out_10), .out_11(demultiplexer_3_out_11),
    .out_12(demultiplexer_3_out_12), .out_13(demultiplexer_3_out_13), .out_14(demultiplexer_3_out_14),
    .out_15(demultiplexer_3_out_15));  // open: sel, in
  Demultiplexer #(.Selector_Bits(4), .Bits(16)) demultiplexer_4 (
    .in(undriven_117), .out_0(demultiplexer_4_out_0), .out_1(demultiplexer_4_out_1),
    .out_2(demultiplexer_4_out_2), .out_3(demultiplexer_4_out_3), .out_4(demultiplexer_4_out_4),
    .out_5(demultiplexer_4_out_5), .out_6(demultiplexer_4_out_6), .out_7(demultiplexer_4_out_7),
    .out_8(demultiplexer_4_out_8), .out_9(demultiplexer_4_out_9), .out_10(demultiplexer_4_out_10),
    .out_11(demultiplexer_4_out_11), .out_12(demultiplexer_4_out_12), .out_13(demultiplexer_4_out_13),
    .out_14(demultiplexer_4_out_14), .out_15(demultiplexer_4_out_15));  // open: sel
  Demultiplexer #(.Selector_Bits(4), .Bits(16)) demultiplexer_5 (
    .out_0({demultiplexer_5_out_0_2, demultiplexer_5_out_0[0]}), .out_1(demultiplexer_5_out_1),
    .out_2(demultiplexer_5_out_2), .out_3(demultiplexer_5_out_3),
    .out_4({demultiplexer_5_out_4, undriven_66[0]}), .out_5(demultiplexer_5_out_5),
    .out_6(demultiplexer_5_out_6), .out_7(demultiplexer_5_out_7),
    .out_8({demultiplexer_5_out_8, undriven_70[0]}), .out_9(demultiplexer_5_out_9),
    .out_10(demultiplexer_5_out_10), .out_11(demultiplexer_5_out_11),
    .out_12({demultiplexer_5_out_12, undriven_74[0]}), .out_13(demultiplexer_5_out_13),
    .out_14(demultiplexer_5_out_14), .out_15(demultiplexer_5_out_15));  // open: sel, in
  Register Z_3 (.C(undriven_103), .en(undriven_104), .Q(Z_3_q));  // open: D
  Register N_3 (.C(undriven_103), .en(undriven_104), .Q(N_3_q));  // open: D
  Register C_3 (.C(undriven_103), .en(undriven_104), .Q(C_3_q));  // open: D
  Register V_3 (.C(undriven_103), .en(undriven_104), .Q(V_3_q));  // open: D
  Register Z_4 (.C(undriven_93), .en(undriven_95), .Q(Z_4_q));  // open: D
  Register N_4 (.C(undriven_93), .en(undriven_95), .Q(N_4_q));  // open: D
  Register C_4 (.C(undriven_93), .en(undriven_95), .Q(C_4_q));  // open: D
  Register V_4 (.C(undriven_93), .en(undriven_95), .Q(V_4_q));  // open: D
  Register Z_5 (.C(undriven_88), .en(undriven_91), .Q(Z_5_q));  // open: D
  Register N_5 (.C(undriven_88), .en(undriven_91), .Q(N_5_q));  // open: D
  Register C_5 (.C(undriven_88), .en(undriven_91), .Q(C_5_q));  // open: D
  Register V_5 (.C(undriven_88), .en(undriven_91), .Q(V_5_q));  // open: D
  Register #(.Bits(16)) t29 (.D(undriven_79), .Q(t29_q));  // open: C, en
  Register #(.Bits(16)) t30 (.D(undriven_66), .Q({t30_q, undriven_53[0]}));  // open: C, en
  Register #(.Bits(16)) t31 (.D(undriven_68), .Q(t31_q));  // open: C, en
  Register #(.Bits(16)) t32 (.D(undriven_70), .Q({t32_q, undriven_27[0]}));  // open: C, en
  Register #(.Bits(16)) t33 (.D(undriven_72), .Q(t33_q));  // open: C, en
  Register #(.Bits(16)) t34 (.D(undriven_74), .Q({t34_q, undriven_31[0]}));  // open: C, en
  Register #(.Bits(16)) t35 (.D(undriven_76), .Q(t35_q));  // open: C, en
  Add #(.Bits(16)) add_6 (.a(multiplexer_46_out), .b(multiplexer_44_out), .c_i(C_3_q), .s(add_6_s), .c_o(add_6_c_o));
  Sub #(.Bits(16)) sub_3 (.a(multiplexer_46_out), .b(multiplexer_44_out), .c_i(C_3_q), .s(sub_3_s), .c_o(sub_3_c_o));
  Mul #(.Bits(16)) mul_3 (.a(multiplexer_46_out), .b(multiplexer_44_out), .mul({mul_3_mul_2, mul_3_mul}));
  Div #(.Bits(16)) div_3 (.a(multiplexer_46_out), .b(multiplexer_44_out), .q(div_3_q), .r(div_3_r));
  assign and_22_out = multiplexer_46_out & multiplexer_44_out;  // And and_22, 16 bits wide
  assign or_15_out = multiplexer_46_out | multiplexer_44_out;  // Or or_15, 16 bits wide
  assign xor_10_out = multiplexer_46_out ^ multiplexer_44_out;  // XOr xor_10, 16 bits wide
  assign nor_4_out = ~(multiplexer_46_out | multiplexer_44_out);  // NOr nor_4, 16 bits wide
  Register #(.Bits(16)) R191 (.D(demultiplexer_4_out_2), .C(undriven_63), .en(undriven_94[16]), .Q(R191_q));
  Register #(.Bits(16)) R193 (.D(demultiplexer_4_out_4), .C(undriven_63), .en(undriven_90[16]), .Q(R193_q));
  Register #(.Bits(16)) R195 (.D(demultiplexer_4_out_6), .C(undriven_63), .en(undriven_87[16]), .Q(R195_q));
  Register #(.Bits(16)) R197 (.D(demultiplexer_4_out_8), .C(undriven_63), .en(undriven_85[16]), .Q(R197_q));
  Register #(.Bits(16)) BUF_4 (.D(demultiplexer_4_out_10), .C(undriven_63), .en(undriven_83[16]), .Q(BUF_4_q));
  Register #(.Bits(16)) STA_4 (.D(demultiplexer_4_out_12), .C(undriven_63), .en(undriven_81[16]), .Q(STA_4_q));
  Register #(.Bits(16)) Link_4 (.D(demultiplexer_4_out_14), .C(undriven_63), .en(undriven_64[16]), .Q(Link_4_q));
  Register #(.Bits(16)) t36 (.D(undriven_80), .Q(t36_q));  // open: C, en
  Register #(.Bits(16)) t37 (.D(undriven_65), .Q(t37_q));  // open: C, en
  Register #(.Bits(16)) t38 (.D(undriven_67), .Q(t38_q));  // open: C, en
  Register #(.Bits(16)) t39 (.D(undriven_69), .Q(t39_q));  // open: C, en
  Register #(.Bits(16)) t40 (.D(undriven_71), .Q(t40_q));  // open: C, en
  Register #(.Bits(16)) t41 (.D(undriven_73), .Q(t41_q));  // open: C, en
  Register #(.Bits(16)) t42 (.D(undriven_75), .Q(t42_q));  // open: C, en
  CounterPreset #(.Bits(16)) PC_4 (
    .en(1'b1), .dir(1'b0), .in(undriven_77), .clr(1'b0), .out(PC_4_out));  // open: C, ld, ovf
  Register #(.Bits(16)) R110 (.D(demultiplexer_3_out_2), .Q(R110_q));  // open: C, en
  Register #(.Bits(16)) R112 (.D(demultiplexer_3_out_4), .Q(R112_q));  // open: C, en
  Register #(.Bits(16)) R114 (.D(demultiplexer_3_out_6), .Q(R114_q));  // open: C, en
  Register #(.Bits(16)) R116 (.D(demultiplexer_3_out_8), .Q(R116_q));  // open: C, en
  Register #(.Bits(16)) BUF_5 (.D(demultiplexer_3_out_10), .Q(BUF_5_q));  // open: C, en
  Register #(.Bits(16)) STA_5 (.D(demultiplexer_3_out_12), .Q(STA_5_q));  // open: C, en
  Register #(.Bits(16)) Link_5 (.D(demultiplexer_3_out_14), .Q(Link_5_q));  // open: C, en
  Add #(.Bits(16)) add_7 (.a(undriven_62), .b(undriven_61), .c_i(C_4_q), .s(add_7_s), .c_o(add_7_c_o));
  Sub #(.Bits(16)) sub_4 (.a(undriven_62), .b(undriven_61), .c_i(C_4_q), .s(sub_4_s), .c_o(sub_4_c_o));
  Mul #(.Bits(16)) mul_4 (.a(undriven_62), .b(undriven_61), .mul({mul_4_mul_2, mul_4_mul}));
  Div #(.Bits(16)) div_4 (.a(undriven_62), .b(undriven_61), .q(div_4_q), .r(div_4_r));
  assign and_23_out = undriven_62 & undriven_61;  // And and_23, 16 bits wide
  assign or_16_out = undriven_62 | undriven_61;  // Or or_16, 16 bits wide
  assign xor_11_out = undriven_62 ^ undriven_61;  // XOr xor_11, 16 bits wide
  assign nor_5_out = ~(undriven_62 | undriven_61);  // NOr nor_5, 16 bits wide
  Add #(.Bits(16)) add_8 (.a(multiplexer_52_out), .b(multiplexer_50_out), .c_i(C_5_q), .s(add_8_s), .c_o(add_8_c_o));
  Sub #(.Bits(16)) sub_5 (.a(multiplexer_52_out), .b(multiplexer_50_out), .c_i(C_5_q), .s(sub_5_s), .c_o(sub_5_c_o));
  Mul #(.Bits(16)) mul_5 (.a(multiplexer_52_out), .b(multiplexer_50_out), .mul({mul_5_mul_2, mul_5_mul}));
  Div #(.Bits(16)) div_5 (.a(multiplexer_52_out), .b(multiplexer_50_out), .q(div_5_q), .r(div_5_r));
  assign and_24_out = multiplexer_52_out & multiplexer_50_out;  // And and_24, 16 bits wide
  assign or_17_out = multiplexer_52_out | multiplexer_50_out;  // Or or_17, 16 bits wide
  assign xor_12_out = multiplexer_52_out ^ multiplexer_50_out;  // XOr xor_12, 16 bits wide
  assign nor_6_out = ~(multiplexer_52_out | multiplexer_50_out);  // NOr nor_6, 16 bits wide
  Register #(.Bits(16)) R109 (.D(demultiplexer_3_out_1), .Q(R109_q));  // open: C, en
  Register #(.Bits(16)) R111 (.D(demultiplexer_3_out_3), .Q(R111_q));  // open: C, en
  Register #(.Bits(16)) R113 (.D(demultiplexer_3_out_5), .Q(R113_q));  // open: C, en
  Register #(.Bits(16)) R115 (.D(demultiplexer_3_out_7), .Q(R115_q));  // open: C, en
  Register #(.Bits(16)) R117 (.D(demultiplexer_3_out_9), .Q(R117_q));  // open: C, en
  Register #(.Bits(16)) RET_4 (.D(demultiplexer_3_out_11), .Q(RET_4_q));  // open: C, en
  Register #(.Bits(16)) Addr_4 (.D(demultiplexer_3_out_13), .Q(Addr_4_q));  // open: C, en
  CounterPreset #(.Bits(16)) PC_5 (
    .en(1'b1), .dir(1'b0), .in(demultiplexer_3_out_15), .out(PC_5_out));  // open: C, ld, clr, ovf
  Register #(.Bits(16)) R190 (.D(demultiplexer_4_out_1), .C(undriven_63), .en(undriven_96[16]), .Q(R190_q));
  Register #(.Bits(16)) R192 (.D(demultiplexer_4_out_3), .C(undriven_63), .en(undriven_92[16]), .Q(R192_q));
  Register #(.Bits(16)) R194 (.D(demultiplexer_4_out_5), .C(undriven_63), .en(undriven_89[16]), .Q(R194_q));
  Register #(.Bits(16)) R196 (.D(demultiplexer_4_out_7), .C(undriven_63), .en(undriven_86[16]), .Q(R196_q));
  Register #(.Bits(16)) R198 (.D(demultiplexer_4_out_9), .C(undriven_63), .en(undriven_84[16]), .Q(R198_q));
  Register #(.Bits(16)) RET_5 (.D(demultiplexer_4_out_11), .C(undriven_63), .en(undriven_82[16]), .Q(RET_5_q));
  Register #(.Bits(16)) Addr_5 (.D(demultiplexer_4_out_13), .C(undriven_63), .en(undriven_78[16]), .Q(Addr_5_q));
  CounterPreset #(.Bits(16)) PC_6 (
    .en(1'b1), .C(undriven_63), .dir(1'b0), .in(demultiplexer_4_out_15), .out(PC_6_out));  // open: ld, clr, ovf
  Multiplexer #(.Selector_Bits(4), .Bits(16)) multiplexer_35 (
    .in_0(undriven_111), .in_1(undriven_112), .in_2(undriven_113), .in_3(undriven_114), .in_4(undriven_115),
    .in_5(undriven_116), .in_6(add_6_s), .in_7(sub_3_s), .in_8(mul_3_mul), .in_9(mul_3_mul_2),
    .in_10(div_3_q), .in_11(div_3_r), .in_12(and_22_out), .in_13(or_15_out), .in_14(xor_10_out),
    .in_15(nor_4_out), .out(multiplexer_35_out));  // open: sel
  Multiplexer #(.Selector_Bits(4), .Bits(16)) multiplexer_36 (
    .in_0(undriven_57), .in_1(undriven_56), .in_2(undriven_55), .in_3(undriven_54), .in_4(undriven_53),
    .in_5(undriven_52), .in_6(undriven_51), .in_7(undriven_26), .in_8(undriven_27), .in_9(undriven_28),
    .in_10(undriven_29), .in_11({undriven_30, undriven_46[0]}), .in_12(undriven_31), .in_13(undriven_32),
    .in_14(undriven_33), .in_15(undriven_34), .out(multiplexer_36_out));  // open: sel
  Multiplexer #(.Selector_Bits(4), .Bits(16)) multiplexer_37 (
    .in_0({undriven_35, undriven_57[0]}), .in_1({undriven_36, undriven_56[0]}),
    .in_2({undriven_37, undriven_55[0]}), .in_3({undriven_38, undriven_54[0]}),
    .in_4({undriven_39, undriven_53[0]}), .in_5({undriven_40, undriven_52[0]}),
    .in_6({undriven_41, undriven_51[0]}), .in_7({undriven_42, undriven_26[0]}),
    .in_8({undriven_43, undriven_27[0]}), .in_9({undriven_44, undriven_28[0]}),
    .in_10({undriven_45, undriven_29[0]}), .in_11(undriven_46), .in_12({undriven_47, undriven_31[0]}),
    .in_13({undriven_48, undriven_32[0]}), .in_14({undriven_49, undriven_33[0]}),
    .in_15({undriven_50, undriven_34[0]}), .out(multiplexer_37_out));  // open: sel
  Demultiplexer #(.Selector_Bits(4), .Bits(16)) demultiplexer_6 (
    .in(multiplexer_35_out), .out_0(demultiplexer_6_out_0), .out_1(demultiplexer_6_out_1),
    .out_2(demultiplexer_6_out_2), .out_3(demultiplexer_6_out_3), .out_4(demultiplexer_6_out_4),
    .out_5(demultiplexer_6_out_5), .out_6(demultiplexer_6_out_6), .out_7(demultiplexer_6_out_7),
    .out_8(demultiplexer_6_out_8), .out_9(demultiplexer_6_out_9), .out_10(demultiplexer_6_out_10),
    .out_11(demultiplexer_6_out_11), .out_12(demultiplexer_6_out_12), .out_13(demultiplexer_6_out_13),
    .out_14(demultiplexer_6_out_14), .out_15(demultiplexer_6_out_15));  // open: sel
  Multiplexer #(.Selector_Bits(4), .Bits(16)) multiplexer_38 (
    .in_0(undriven_105), .in_1(undriven_106), .in_2(undriven_107), .in_3(undriven_108), .in_4(undriven_109),
    .in_5(undriven_110), .in_6(add_7_s), .in_7(sub_4_s), .in_8(mul_4_mul), .in_9(mul_4_mul_2),
    .in_10(div_4_q), .in_11(div_4_r), .in_12(and_23_out), .in_13(or_16_out), .in_14(xor_11_out),
    .in_15(nor_5_out), .out(multiplexer_38_out));  // open: sel
  Multiplexer #(.Selector_Bits(4), .Bits(16)) multiplexer_39 (
    .in_0(undriven_102), .in_1(undriven_101), .in_2(undriven_100), .in_3(undriven_99), .in_4(undriven_98),
    .in_5(undriven_97), .in_6(add_8_s), .in_7(sub_5_s), .in_8(mul_5_mul), .in_9(mul_5_mul_2),
    .in_10(div_5_q), .in_11(div_5_r), .in_12(and_24_out), .in_13(or_17_out), .in_14(xor_12_out),
    .in_15(nor_6_out), .out(multiplexer_39_out));  // open: sel
  Demultiplexer #(.Selector_Bits(4), .Bits(16)) demultiplexer_7 (
    .in(multiplexer_38_out), .out_0(demultiplexer_7_out_0), .out_1(demultiplexer_7_out_1),
    .out_2(demultiplexer_7_out_2), .out_3(demultiplexer_7_out_3), .out_4(demultiplexer_7_out_4),
    .out_5(demultiplexer_7_out_5), .out_6(demultiplexer_7_out_6), .out_7(demultiplexer_7_out_7),
    .out_8(demultiplexer_7_out_8), .out_9(demultiplexer_7_out_9), .out_10(demultiplexer_7_out_10),
    .out_11(demultiplexer_7_out_11), .out_12(demultiplexer_7_out_12), .out_13(demultiplexer_7_out_13),
    .out_14(demultiplexer_7_out_14), .out_15(demultiplexer_7_out_15));  // open: sel
  Demultiplexer #(.Selector_Bits(4), .Bits(16)) demultiplexer_8 (
    .in(multiplexer_39_out), .out_0(demultiplexer_8_out_0), .out_1(demultiplexer_8_out_1),
    .out_2(demultiplexer_8_out_2), .out_3(demultiplexer_8_out_3), .out_4(demultiplexer_8_out_4),
    .out_5(demultiplexer_8_out_5), .out_6(demultiplexer_8_out_6), .out_7(demultiplexer_8_out_7),
    .out_8(demultiplexer_8_out_8), .out_9(demultiplexer_8_out_9), .out_10(demultiplexer_8_out_10),
    .out_11(demultiplexer_8_out_11), .out_12(demultiplexer_8_out_12), .out_13(demultiplexer_8_out_13),
    .out_14(demultiplexer_8_out_14), .out_15(demultiplexer_8_out_15));  // open: sel
  Demultiplexer #(.Selector_Bits(4), .Bits(16)) demultiplexer_9 (
    .out_0(demultiplexer_9_out_0), .out_1(demultiplexer_9_out_1), .out_2(demultiplexer_9_out_2),
    .out_3(demultiplexer_9_out_3), .out_4(demultiplexer_9_out_4), .out_5(demultiplexer_9_out_5),
    .out_6(demultiplexer_9_out_6), .out_7(demultiplexer_9_out_7), .out_8(demultiplexer_9_out_8),
    .out_9(demultiplexer_9_out_9), .out_10(demultiplexer_9_out_10), .out_11(demultiplexer_9_out_11),
    .out_12(demultiplexer_9_out_12), .out_13(demultiplexer_9_out_13), .out_14(demultiplexer_9_out_14),
    .out_15(demultiplexer_9_out_15));  // open: sel, in
  Multiplexer #(.Selector_Bits(4), .Bits(16)) multiplexer_40 (
    .sel(undriven_60), .in_0({16{1'b0}}), .in_1(R190_q), .in_2(R191_q), .in_3(R192_q), .in_4(R193_q),
    .in_5(R194_q), .in_6(R195_q), .in_7(R196_q), .in_8(R197_q), .in_9(R198_q), .in_10(BUF_4_q),
    .in_11(RET_5_q), .in_12(STA_4_q), .in_13(Addr_5_q), .in_14(Link_4_q), .in_15(PC_6_out),
    .out(multiplexer_40_out));
  Multiplexer #(.Selector_Bits(4), .Bits(16)) multiplexer_41 (
    .in_1({16{1'b0}}), .in_2(R109_q), .in_3(R110_q), .in_4(R111_q), .in_5(R112_q), .in_6(R113_q),
    .in_7(R114_q), .in_8(R115_q), .in_9(R116_q), .in_10(R117_q), .in_11(BUF_5_q), .in_12(RET_4_q),
    .in_13(STA_5_q), .in_14(Addr_4_q), .in_15(Link_5_q));  // open: sel, in_0, out
  Register #(.Bits(16)) R155 (.D(demultiplexer_6_out_2), .C(undriven_103), .Q(R155_q));  // open: en
  Register #(.Bits(16)) R157 (.D(demultiplexer_6_out_4), .C(undriven_103), .Q(R157_q));  // open: en
  Register #(.Bits(16)) R159 (.D(demultiplexer_6_out_6), .C(undriven_103), .Q(R159_q));  // open: en
  Register #(.Bits(16)) R161 (.D(demultiplexer_6_out_8), .C(undriven_103), .Q(R161_q));  // open: en
  Register #(.Bits(16)) BUF_6 (.D(demultiplexer_6_out_10), .C(undriven_103), .Q(BUF_6_q));  // open: en
  Register #(.Bits(16)) STA_6 (.D(demultiplexer_6_out_12), .C(undriven_103), .Q(STA_6_q));  // open: en
  Register #(.Bits(16)) Link_6 (.D(demultiplexer_6_out_14), .C(undriven_103), .Q(Link_6_q));  // open: en
  Register #(.Bits(16)) R154 (.D(demultiplexer_6_out_1), .C(undriven_103), .Q(R154_q));  // open: en
  Register #(.Bits(16)) R156 (.D(demultiplexer_6_out_3), .C(undriven_103), .Q(R156_q));  // open: en
  Register #(.Bits(16)) R158 (.D(demultiplexer_6_out_5), .C(undriven_103), .Q(R158_q));  // open: en
  Register #(.Bits(16)) R160 (.D(demultiplexer_6_out_7), .C(undriven_103), .Q(R160_q));  // open: en
  Register #(.Bits(16)) R162 (.D(demultiplexer_6_out_9), .C(undriven_103), .Q(R162_q));  // open: en
  Register #(.Bits(16)) RET_6 (.D(demultiplexer_6_out_11), .C(undriven_103), .Q(RET_6_q));  // open: en
  Register #(.Bits(16)) Addr_6 (.D(demultiplexer_6_out_13), .C(undriven_103), .Q(Addr_6_q));  // open: en
  CounterPreset #(.Bits(16)) PC_7 (
    .en(1'b1), .dir(1'b0), .in(demultiplexer_6_out_15), .clr(1'b0), .out(PC_7_out));  // open: C, ld, ovf
  Register #(.Bits(16)) R173 (.D(demultiplexer_7_out_2), .C(undriven_25), .Q(R173_q));  // open: en
  Register #(.Bits(16)) R175 (.D(demultiplexer_7_out_4), .C(undriven_25), .Q(R175_q));  // open: en
  Register #(.Bits(16)) R177 (.D(demultiplexer_7_out_6), .C(undriven_25), .Q(R177_q));  // open: en
  Register #(.Bits(16)) R179 (.D(demultiplexer_7_out_8), .C(undriven_25), .Q(R179_q));  // open: en
  Register #(.Bits(16)) BUF_7 (.D(demultiplexer_7_out_10), .C(undriven_25), .Q(BUF_7_q));  // open: en
  Register #(.Bits(16)) STA_7 (.D(demultiplexer_7_out_12), .C(undriven_25), .Q(STA_7_q));  // open: en
  Register #(.Bits(16)) Link_7 (.D(demultiplexer_7_out_14), .C(undriven_25), .Q(Link_7_q));  // open: en
  Register #(.Bits(16)) R146 (.D(demultiplexer_8_out_2), .C(undriven_88), .Q(R146_q));  // open: en
  Register #(.Bits(16)) R148 (.D(demultiplexer_8_out_4), .C(undriven_88), .Q(R148_q));  // open: en
  Register #(.Bits(16)) R150 (.D(demultiplexer_8_out_6), .C(undriven_88), .Q(R150_q));  // open: en
  Register #(.Bits(16)) R152 (.D(demultiplexer_8_out_8), .C(undriven_88), .Q(R152_q));  // open: en
  Register #(.Bits(16)) BUF_8 (.D(demultiplexer_8_out_10), .C(undriven_88), .Q(BUF_8_q));  // open: en
  Register #(.Bits(16)) STA_8 (.D(demultiplexer_8_out_12), .C(undriven_88), .Q(STA_8_q));  // open: en
  Register #(.Bits(16)) Link_8 (.D(demultiplexer_8_out_14), .C(undriven_88), .Q(Link_8_q));  // open: en
  Register #(.Bits(16)) R172 (.D(demultiplexer_7_out_1), .C(undriven_25), .Q(R172_q));  // open: en
  Register #(.Bits(16)) R174 (.D(demultiplexer_7_out_3), .C(undriven_25), .Q(R174_q));  // open: en
  Register #(.Bits(16)) R176 (.D(demultiplexer_7_out_5), .C(undriven_25), .Q(R176_q));  // open: en
  Register #(.Bits(16)) R178 (.D(demultiplexer_7_out_7), .C(undriven_25), .Q(R178_q));  // open: en
  Register #(.Bits(16)) R180 (.D(demultiplexer_7_out_9), .C(undriven_25), .Q(R180_q));  // open: en
  Register #(.Bits(16)) RET_7 (.D(demultiplexer_7_out_11), .C(undriven_25), .Q(RET_7_q));  // open: en
  Register #(.Bits(16)) Addr_7 (.D(demultiplexer_7_out_13), .C(undriven_25), .Q(Addr_7_q));  // open: en
  CounterPreset #(.Bits(16)) PC_8 (
    .en(1'b1), .dir(1'b0), .in(demultiplexer_7_out_15), .clr(1'b0), .out(PC_8_out));  // open: C, ld, ovf
  Register #(.Bits(16)) R145 (.D(demultiplexer_8_out_1), .C(undriven_88), .Q(R145_q));  // open: en
  Register #(.Bits(16)) R147 (.D(demultiplexer_8_out_3), .C(undriven_88), .Q(R147_q));  // open: en
  Register #(.Bits(16)) R149 (.D(demultiplexer_8_out_5), .C(undriven_88), .Q(R149_q));  // open: en
  Register #(.Bits(16)) R151 (.D(demultiplexer_8_out_7), .C(undriven_88), .Q(R151_q));  // open: en
  Register #(.Bits(16)) R153 (.D(demultiplexer_8_out_9), .C(undriven_88), .Q(R153_q));  // open: en
  Register #(.Bits(16)) RET_8 (.D(demultiplexer_8_out_11), .C(undriven_88), .Q(RET_8_q));  // open: en
  Register #(.Bits(16)) Addr_8 (.D(demultiplexer_8_out_13), .C(undriven_88), .Q(Addr_8_q));  // open: en
  CounterPreset #(.Bits(16)) PC_9 (
    .en(1'b1), .dir(1'b0), .in(demultiplexer_8_out_15), .clr(1'b0), .out(PC_9_out));  // open: C, ld, ovf
  Multiplexer #(.Selector_Bits(4), .Bits(16)) multiplexer_42 (
    .sel(undriven_59), .in_0({16{1'b0}}), .in_1(R190_q), .in_2(R191_q), .in_3(R192_q), .in_4(R193_q),
    .in_5(R194_q), .in_6(R195_q), .in_7(R196_q), .in_8(R197_q), .in_9(R198_q), .in_10(BUF_4_q),
    .in_11(RET_5_q), .in_12(STA_4_q), .in_13(Addr_5_q), .in_14(Link_4_q), .in_15(PC_6_out),
    .out(multiplexer_42_out));
  Register #(.Bits(16)) R119 (.D(demultiplexer_9_out_2), .Q(R119_q));  // open: C, en
  Register #(.Bits(16)) R121 (.D(demultiplexer_9_out_4), .Q(R121_q));  // open: C, en
  Register #(.Bits(16)) R123 (.D(demultiplexer_9_out_6), .Q(R123_q));  // open: C, en
  Register #(.Bits(16)) R125 (.D(demultiplexer_9_out_8), .Q(R125_q));  // open: C, en
  Register #(.Bits(16)) BUF_9 (.D(demultiplexer_9_out_10), .Q(BUF_9_q));  // open: C, en
  Register #(.Bits(16)) STA_9 (.D(demultiplexer_9_out_12), .Q(STA_9_q));  // open: C, en
  Register #(.Bits(16)) Link_9 (.D(demultiplexer_9_out_14), .Q(Link_9_q));  // open: C, en
  Multiplexer #(.Selector_Bits(4), .Bits(16)) multiplexer_43 (
    .in_1({16{1'b0}}), .in_2(R109_q), .in_3(R110_q), .in_4(R111_q), .in_5(R112_q), .in_6(R113_q),
    .in_7(R114_q), .in_8(R115_q), .in_9(R116_q), .in_10(R117_q), .in_11(BUF_5_q), .in_12(RET_4_q),
    .in_13(STA_5_q), .in_14(Addr_4_q), .in_15(Link_5_q));  // open: sel, in_0, out
  Multiplexer #(.Selector_Bits(4), .Bits(16)) multiplexer_44 (
    .in_0({16{1'b0}}), .in_1(R154_q), .in_2(R155_q), .in_3(R156_q), .in_4(R157_q), .in_5(R158_q),
    .in_6(R159_q), .in_7(R160_q), .in_8(R161_q), .in_9(R162_q), .in_10(BUF_6_q), .in_11(RET_6_q),
    .in_12(STA_6_q), .in_13(Addr_6_q), .in_14(Link_6_q), .in_15(PC_7_out), .out(multiplexer_44_out));  // open: sel
  Multiplexer #(.Selector_Bits(4), .Bits(16)) multiplexer_45 (
    .in_0({16{1'b0}}), .in_1(R154_q), .in_2(R155_q), .in_3(R156_q), .in_4(R157_q), .in_5(R158_q),
    .in_6(R159_q), .in_7(R160_q), .in_8(R161_q), .in_9(R162_q), .in_10(BUF_6_q), .in_11(RET_6_q),
    .in_12(STA_6_q), .in_13(Addr_6_q), .in_14(Link_6_q), .in_15(PC_7_out), .out(multiplexer_45_out));  // open: sel
  Multiplexer #(.Selector_Bits(4), .Bits(16)) multiplexer_46 (
    .in_0({16{1'b0}}), .in_1(R154_q), .in_2(R155_q), .in_3(R156_q), .in_4(R157_q), .in_5(R158_q),
    .in_6(R159_q), .in_7(R160_q), .in_8(R161_q), .in_9(R162_q), .in_10(BUF_6_q), .in_11(RET_6_q),
    .in_12(STA_6_q), .in_13(Addr_6_q), .in_14(Link_6_q), .in_15(PC_7_out), .out(multiplexer_46_out));  // open: sel
  Register #(.Bits(16)) R118 (.D(demultiplexer_9_out_1), .Q(R118_q));  // open: C, en
  Register #(.Bits(16)) R120 (.D(demultiplexer_9_out_3), .Q(R120_q));  // open: C, en
  Register #(.Bits(16)) R122 (.D(demultiplexer_9_out_5), .Q(R122_q));  // open: C, en
  Register #(.Bits(16)) R124 (.D(demultiplexer_9_out_7), .Q(R124_q));  // open: C, en
  Register #(.Bits(16)) R126 (.D(demultiplexer_9_out_9), .Q(R126_q));  // open: C, en
  Register #(.Bits(16)) RET_9 (.D(demultiplexer_9_out_11), .Q(RET_9_q));  // open: C, en
  Register #(.Bits(16)) Addr_9 (.D(demultiplexer_9_out_13), .Q(Addr_9_q));  // open: C, en
  CounterPreset #(.Bits(16)) PC_10 (
    .en(1'b1), .dir(1'b0), .in(demultiplexer_9_out_15), .out(PC_10_out));  // open: C, ld, clr, ovf
  Multiplexer #(.Selector_Bits(4), .Bits(16)) multiplexer_47 (
    .in_0({16{1'b0}}), .in_1(R172_q), .in_2(R173_q), .in_3(R174_q), .in_4(R175_q), .in_5(R176_q),
    .in_6(R177_q), .in_7(R178_q), .in_8(R179_q), .in_9(R180_q), .in_10(BUF_7_q), .in_11(RET_7_q),
    .in_12(STA_7_q), .in_13(Addr_7_q), .in_14(Link_7_q), .in_15(PC_8_out), .out(multiplexer_47_out));  // open: sel
  Multiplexer #(.Selector_Bits(4), .Bits(16)) multiplexer_48 (
    .in_0({16{1'b0}}), .in_1(R172_q), .in_2(R173_q), .in_3(R174_q), .in_4(R175_q), .in_5(R176_q),
    .in_6(R177_q), .in_7(R178_q), .in_8(R179_q), .in_9(R180_q), .in_10(BUF_7_q), .in_11(RET_7_q),
    .in_12(STA_7_q), .in_13(Addr_7_q), .in_14(Link_7_q), .in_15(PC_8_out), .out(multiplexer_48_out));  // open: sel
  Multiplexer #(.Selector_Bits(4), .Bits(16)) multiplexer_49 (
    .in_0({16{1'b0}}), .in_1(R172_q), .in_2(R173_q), .in_3(R174_q), .in_4(R175_q), .in_5(R176_q),
    .in_6(R177_q), .in_7(R178_q), .in_8(R179_q), .in_9(R180_q), .in_10(BUF_7_q), .in_11(RET_7_q),
    .in_12(STA_7_q), .in_13(Addr_7_q), .in_14(Link_7_q), .in_15(PC_8_out), .out(multiplexer_49_out));  // open: sel
  Multiplexer #(.Selector_Bits(4), .Bits(16)) multiplexer_50 (
    .in_0({16{1'b0}}), .in_1(R145_q), .in_2(R146_q), .in_3(R147_q), .in_4(R148_q), .in_5(R149_q),
    .in_6(R150_q), .in_7(R151_q), .in_8(R152_q), .in_9(R153_q), .in_10(BUF_8_q), .in_11(RET_8_q),
    .in_12(STA_8_q), .in_13(Addr_8_q), .in_14(Link_8_q), .in_15(PC_9_out), .out(multiplexer_50_out));  // open: sel
  Multiplexer #(.Selector_Bits(4), .Bits(16)) multiplexer_51 (
    .in_0({16{1'b0}}), .in_1(R145_q), .in_2(R146_q), .in_3(R147_q), .in_4(R148_q), .in_5(R149_q),
    .in_6(R150_q), .in_7(R151_q), .in_8(R152_q), .in_9(R153_q), .in_10(BUF_8_q), .in_11(RET_8_q),
    .in_12(STA_8_q), .in_13(Addr_8_q), .in_14(Link_8_q), .in_15(PC_9_out), .out(multiplexer_51_out));  // open: sel
  Multiplexer #(.Selector_Bits(4), .Bits(16)) multiplexer_52 (
    .in_0({16{1'b0}}), .in_1(R145_q), .in_2(R146_q), .in_3(R147_q), .in_4(R148_q), .in_5(R149_q),
    .in_6(R150_q), .in_7(R151_q), .in_8(R152_q), .in_9(R153_q), .in_10(BUF_8_q), .in_11(RET_8_q),
    .in_12(STA_8_q), .in_13(Addr_8_q), .in_14(Link_8_q), .in_15(PC_9_out), .out(multiplexer_52_out));  // open: sel
  Multiplexer #(.Selector_Bits(4), .Bits(16)) multiplexer_53 (
    .in_1({16{1'b0}}), .in_2(R109_q), .in_3(R110_q), .in_4(R111_q), .in_5(R112_q), .in_6(R113_q),
    .in_7(R114_q), .in_8(R115_q), .in_9(R116_q), .in_10(R117_q), .in_11(BUF_5_q), .in_12(RET_4_q),
    .in_13(STA_5_q), .in_14(Addr_4_q), .in_15(Link_5_q));  // open: sel, in_0, out
  Multiplexer #(.Selector_Bits(4), .Bits(16)) multiplexer_54 (
    .sel(undriven_58), .in_0({16{1'b0}}), .in_1(R190_q), .in_2(R191_q), .in_3(R192_q), .in_4(R193_q),
    .in_5(R194_q), .in_6(R195_q), .in_7(R196_q), .in_8(R197_q), .in_9(R198_q), .in_10(BUF_4_q),
    .in_11(RET_5_q), .in_12(STA_4_q), .in_13(Addr_5_q), .in_14(Link_4_q), .in_15(PC_6_out),
    .out(multiplexer_54_out));
  Register Z_6 (.C(undriven_17), .en(undriven_18), .Q(Z_6_q));  // open: D
  Register N_6 (.C(undriven_17), .en(undriven_18), .Q(N_6_q));  // open: D
  Register C_6 (.C(undriven_17), .en(undriven_18), .Q(C_6_q));  // open: D
  Register V_6 (.C(undriven_17), .en(undriven_18), .Q(V_6_q));  // open: D
  Multiplexer #(.Selector_Bits(4), .Bits(16)) multiplexer_55 (
    .in_0({16{1'b0}}), .in_1(R118_q), .in_2(R119_q), .in_3(R120_q), .in_4(R121_q), .in_5(R122_q),
    .in_6(R123_q), .in_7(R124_q), .in_8(R125_q), .in_9(R126_q), .in_10(BUF_9_q), .in_11(RET_9_q),
    .in_12(STA_9_q), .in_13(Addr_9_q), .in_14(Link_9_q), .in_15(PC_10_out), .out(multiplexer_55_out));  // open: sel
  Multiplexer #(.Selector_Bits(4), .Bits(16)) multiplexer_56 (
    .in_0({16{1'b0}}), .in_1(R118_q), .in_2(R119_q), .in_3(R120_q), .in_4(R121_q), .in_5(R122_q),
    .in_6(R123_q), .in_7(R124_q), .in_8(R125_q), .in_9(R126_q), .in_10(BUF_9_q), .in_11(RET_9_q),
    .in_12(STA_9_q), .in_13(Addr_9_q), .in_14(Link_9_q), .in_15(PC_10_out), .out(multiplexer_56_out));  // open: sel
  Demultiplexer #(.Selector_Bits(4), .Bits(16)) demultiplexer_10 (
    .in(undriven_16), .out_0(demultiplexer_10_out_0), .out_1(demultiplexer_10_out_1),
    .out_2(demultiplexer_10_out_2), .out_3(demultiplexer_10_out_3), .out_4(demultiplexer_10_out_4),
    .out_5(demultiplexer_10_out_5), .out_6(demultiplexer_10_out_6), .out_7(demultiplexer_10_out_7),
    .out_8(demultiplexer_10_out_8), .out_9(demultiplexer_10_out_9), .out_10(demultiplexer_10_out_10),
    .out_11(demultiplexer_10_out_11), .out_12(demultiplexer_10_out_12), .out_13(demultiplexer_10_out_13),
    .out_14(demultiplexer_10_out_14), .out_15(demultiplexer_10_out_15));  // open: sel
  Add #(.Bits(16)) add_9 (.a(multiplexer_62_out), .b(multiplexer_61_out), .c_i(C_6_q), .s(add_9_s), .c_o(add_9_c_o));
  Sub #(.Bits(16)) sub_6 (.a(multiplexer_62_out), .b(multiplexer_61_out), .c_i(C_6_q), .s(sub_6_s), .c_o(sub_6_c_o));
  Mul #(.Bits(16)) mul_6 (.a(multiplexer_62_out), .b(multiplexer_61_out), .mul({mul_6_mul_2, mul_6_mul}));
  Div #(.Bits(16)) div_6 (.a(multiplexer_62_out), .b(multiplexer_61_out), .q(div_6_q), .r(div_6_r));
  assign and_25_out = multiplexer_62_out & multiplexer_61_out;  // And and_25, 16 bits wide
  assign or_18_out = multiplexer_62_out | multiplexer_61_out;  // Or or_18, 16 bits wide
  assign xor_13_out = multiplexer_62_out ^ multiplexer_61_out;  // XOr xor_13, 16 bits wide
  assign nor_7_out = ~(multiplexer_62_out | multiplexer_61_out);  // NOr nor_7, 16 bits wide
  Register #(.Bits(16)) R182 (.D(demultiplexer_10_out_2), .C(undriven), .en(undriven_14[16]), .Q(R182_q));
  Register #(.Bits(16)) R184 (.D(demultiplexer_10_out_4), .C(undriven), .en(undriven_12[16]), .Q(R184_q));
  Register #(.Bits(16)) R186 (.D(demultiplexer_10_out_6), .C(undriven), .en(undriven_10[16]), .Q(R186_q));
  Register #(.Bits(16)) R188 (.D(demultiplexer_10_out_8), .C(undriven), .en(undriven_8[16]), .Q(R188_q));
  Register #(.Bits(16)) BUF_10 (.D(demultiplexer_10_out_10), .C(undriven), .en(undriven_6[16]), .Q(BUF_10_q));
  Register #(.Bits(16)) STA_10 (.D(demultiplexer_10_out_12), .C(undriven), .en(undriven_4[16]), .Q(STA_10_q));
  Register #(.Bits(16)) Link_10 (.D(demultiplexer_10_out_14), .C(undriven), .en(undriven_2[16]), .Q(Link_10_q));
  Multiplexer #(.Selector_Bits(4), .Bits(16)) multiplexer_57 (
    .in_0(undriven_24), .in_1(undriven_23), .in_2(undriven_22), .in_3(undriven_21), .in_4(undriven_20),
    .in_5(undriven_19), .in_6(add_9_s), .in_7(sub_6_s), .in_8(mul_6_mul), .in_9(mul_6_mul_2),
    .in_10(div_6_q), .in_11(div_6_r), .in_12(and_25_out), .in_13(or_18_out), .in_14(xor_13_out),
    .in_15(nor_7_out), .out(multiplexer_57_out));  // open: sel
  Demultiplexer #(.Selector_Bits(4), .Bits(16)) demultiplexer_11 (
    .in(multiplexer_57_out), .out_0(demultiplexer_11_out_0), .out_1(demultiplexer_11_out_1),
    .out_2(demultiplexer_11_out_2), .out_3(demultiplexer_11_out_3), .out_4(demultiplexer_11_out_4),
    .out_5(demultiplexer_11_out_5), .out_6(demultiplexer_11_out_6), .out_7(demultiplexer_11_out_7),
    .out_8(demultiplexer_11_out_8), .out_9(demultiplexer_11_out_9), .out_10(demultiplexer_11_out_10),
    .out_11(demultiplexer_11_out_11), .out_12(demultiplexer_11_out_12), .out_13(demultiplexer_11_out_13),
    .out_14(demultiplexer_11_out_14), .out_15(demultiplexer_11_out_15));  // open: sel
  Register #(.Bits(16)) R181 (.D(demultiplexer_10_out_1), .C(undriven), .en(undriven_15[16]), .Q(R181_q));
  Register #(.Bits(16)) R183 (.D(demultiplexer_10_out_3), .C(undriven), .en(undriven_13[16]), .Q(R183_q));
  Register #(.Bits(16)) R185 (.D(demultiplexer_10_out_5), .C(undriven), .en(undriven_11[16]), .Q(R185_q));
  Register #(.Bits(16)) R187 (.D(demultiplexer_10_out_7), .C(undriven), .en(undriven_9[16]), .Q(R187_q));
  Register #(.Bits(16)) R189 (.D(demultiplexer_10_out_9), .C(undriven), .en(undriven_7[16]), .Q(R189_q));
  Register #(.Bits(16)) RET_10 (.D(demultiplexer_10_out_11), .C(undriven), .en(undriven_5[16]), .Q(RET_10_q));
  Register #(.Bits(16)) Addr_10 (.D(demultiplexer_10_out_13), .C(undriven), .en(undriven_3[16]), .Q(Addr_10_q));
  CounterPreset #(.Bits(16)) PC_11 (
    .en(1'b1), .C(undriven), .dir(1'b0), .in(demultiplexer_10_out_15), .out(PC_11_out));  // open: ld, clr, ovf
  Register #(.Bits(16)) R92 (.D(demultiplexer_11_out_2), .C(undriven_17), .Q(R92_q));  // open: en
  Register #(.Bits(16)) R94 (.D(demultiplexer_11_out_4), .C(undriven_17), .Q(R94_q));  // open: en
  Register #(.Bits(16)) R96 (.D(demultiplexer_11_out_6), .C(undriven_17), .Q(R96_q));  // open: en
  Register #(.Bits(16)) R98 (.D(demultiplexer_11_out_8), .C(undriven_17), .Q(R98_q));  // open: en
  Register #(.Bits(16)) BUF_11 (.D(demultiplexer_11_out_10), .C(undriven_17), .Q(BUF_11_q));  // open: en
  Register #(.Bits(16)) STA_11 (.D(demultiplexer_11_out_12), .C(undriven_17), .Q(STA_11_q));  // open: en
  Register #(.Bits(16)) Link_11 (.D(demultiplexer_11_out_14), .C(undriven_17), .Q(Link_11_q));  // open: en
  Register #(.Bits(16)) R91 (.D(demultiplexer_11_out_1), .C(undriven_17), .Q(R91_q));  // open: en
  Register #(.Bits(16)) R93 (.D(demultiplexer_11_out_3), .C(undriven_17), .Q(R93_q));  // open: en
  Register #(.Bits(16)) R95 (.D(demultiplexer_11_out_5), .C(undriven_17), .Q(R95_q));  // open: en
  Register #(.Bits(16)) R97 (.D(demultiplexer_11_out_7), .C(undriven_17), .Q(R97_q));  // open: en
  Register #(.Bits(16)) R99 (.D(demultiplexer_11_out_9), .C(undriven_17), .Q(R99_q));  // open: en
  Register #(.Bits(16)) RET_11 (.D(demultiplexer_11_out_11), .C(undriven_17), .Q(RET_11_q));  // open: en
  Register #(.Bits(16)) Addr_11 (.D(demultiplexer_11_out_13), .C(undriven_17), .Q(Addr_11_q));  // open: en
  CounterPreset #(.Bits(16)) PC_12 (
    .en(1'b1), .dir(1'b0), .in(demultiplexer_11_out_15), .clr(1'b0), .out(PC_12_out));  // open: C, ld, ovf
  Multiplexer #(.Selector_Bits(4), .Bits(16)) multiplexer_58 (
    .in_0({16{1'b0}}), .in_1(R181_q), .in_2(R182_q), .in_3(R183_q), .in_4(R184_q), .in_5(R185_q),
    .in_6(R186_q), .in_7(R187_q), .in_8(R188_q), .in_9(R189_q), .in_10(BUF_10_q), .in_11(RET_10_q),
    .in_12(STA_10_q), .in_13(Addr_10_q), .in_14(Link_10_q), .in_15(PC_11_out), .out(multiplexer_58_out));  // open: sel
  Multiplexer #(.Selector_Bits(4), .Bits(16)) multiplexer_59 (
    .in_0({16{1'b0}}), .in_1(R181_q), .in_2(R182_q), .in_3(R183_q), .in_4(R184_q), .in_5(R185_q),
    .in_6(R186_q), .in_7(R187_q), .in_8(R188_q), .in_9(R189_q), .in_10(BUF_10_q), .in_11(RET_10_q),
    .in_12(STA_10_q), .in_13(Addr_10_q), .in_14(Link_10_q), .in_15(PC_11_out), .out(multiplexer_59_out));  // open: sel
  Multiplexer #(.Selector_Bits(4), .Bits(16)) multiplexer_60 (
    .in_0({16{1'b0}}), .in_1(R181_q), .in_2(R182_q), .in_3(R183_q), .in_4(R184_q), .in_5(R185_q),
    .in_6(R186_q), .in_7(R187_q), .in_8(R188_q), .in_9(R189_q), .in_10(BUF_10_q), .in_11(RET_10_q),
    .in_12(STA_10_q), .in_13(Addr_10_q), .in_14(Link_10_q), .in_15(PC_11_out), .out(multiplexer_60_out));  // open: sel
  Multiplexer #(.Selector_Bits(4), .Bits(16)) multiplexer_61 (
    .in_0({16{1'b0}}), .in_1(R91_q), .in_2(R92_q), .in_3(R93_q), .in_4(R94_q), .in_5(R95_q), .in_6(R96_q),
    .in_7(R97_q), .in_8(R98_q), .in_9(R99_q), .in_10(BUF_11_q), .in_11(RET_11_q), .in_12(STA_11_q),
    .in_13(Addr_11_q), .in_14(Link_11_q), .in_15(PC_12_out), .out(multiplexer_61_out));  // open: sel
  Multiplexer #(.Selector_Bits(4), .Bits(16)) multiplexer_62 (
    .in_0({16{1'b0}}), .in_1(R91_q), .in_2(R92_q), .in_3(R93_q), .in_4(R94_q), .in_5(R95_q), .in_6(R96_q),
    .in_7(R97_q), .in_8(R98_q), .in_9(R99_q), .in_10(BUF_11_q), .in_11(RET_11_q), .in_12(STA_11_q),
    .in_13(Addr_11_q), .in_14(Link_11_q), .in_15(PC_12_out), .out(multiplexer_62_out));  // open: sel
  // Pins of 16 and 17 bits meet at {1'b1, multiplexer_12_out}
  // Pins of 16 and 17 bits meet at {undriven_145[16], demultiplexer_2_out_1}
  // Pins of 16 and 17 bits meet at {undriven_143[16], demultiplexer_2_out_2}
  // Pins of 16 and 17 bits meet at {undriven_141[16], demultiplexer_2_out_3}
  // Pins of 16 and 17 bits meet at {undriven_139[16], demultiplexer_2_out_4}
  // Pins of 16 and 17 bits meet at {undriven_137[16], demultiplexer_2_out_5}
  // Pins of 16 and 17 bits meet at {undriven_135[16], demultiplexer_2_out_6}
  // Pins of 16 and 17 bits meet at {undriven_133[16], demultiplexer_2_out_7}
  // Pins of 16 and 17 bits meet at {undriven_131[16], demultiplexer_2_out_8}
  // Pins of 16 and 17 bits meet at {undriven_129[16], demultiplexer_2_out_9}
  // Pins of 16 and 17 bits meet at {undriven_127[16], demultiplexer_2_out_10}
  // Pins of 16 and 17 bits meet at {undriven_125[16], demultiplexer_2_out_11}

  // Notes on the sheet:
  //   CLK: Hz: 10
  //   CLK_2: Hz: 10
  //   INSTR loads fibbo.asm.hex
  //   contents of MEM (hex, n*v repeats v):
  //   b520
  //   CONTROL UNIT
  //   OPERAND
  //   OPCODE
  //   CLK
  //   Rm
  //   Rn
  //   Rd
  //   IMM8
  //   LDR
  //   MemWE
  //   NZCV EN
  //   CV SEL
  //   FLAG ON
  //   FLAG RESET
  //   CONDITIONS
  //   N
  //   Z
  //   C
  //   V
  //   INSTR_2 loads fibbo.asm.hex
  //   contents of MEM_2 (hex, n*v repeats v):
  //   b520
  //   NS
  //   NC
  //   ZS
  //   ZC
  //   CS
  //   CC
  //   VS
  //   VC
  //   SM
  //   HI
  //   LT
  //   GT
  //   LE
  //   GE
  //   FC
  //   AL
  //   NOR
  //   XOR
  //   CMOVE
  //   OPRAND
  //   RnWE
  //   NZCV ON
  //   NZCV RST
  //   INSERT
  //   SHIFT
  //   OP
  //   EQUAL
  //   NOT EQ
  //   SMALLER
  //   HIGER EQ
  //   CARRY
  //   NOT C
  //   OV FLOW
  //   NOT OV
  //   U SMALLER
  //   U HIGHER
  //   HIGHER
  //   SMALLER EQ
  //   HIGHER EQ
  //   FLAG CLEAR
  //   ALWAYS
  //   CND
  //   Dd
  //   Dn
  //   PC
  //   BRANCH
  //   POST IDX
  //   MVS
  //   DnIN
  //   Dm
  //   MOV
  //   CNS
  //   SFT
  //   NZCV CONTROL UNIT
  //   DdIN
  //   ALU
  //   NZCV SELECT BIT
  //   NZCV REGISTERS
  //   REGISTER FILE
  //   STR
  //   ADD
  //   SUB
  //   MUL
  //   LML
  //   DIV
  //   MOD
  //   AND
  //   ORR
  //   WE
  //   Didx
  //   Zero
  //   Buffer Register
  //   Return Register
  //   Stack Pointer
  //   Address Register
  //   Link Register
  //   Program Counter
endmodule
