// Digital circuit Simplic.dig as structural Verilog
module Simplic (
  input  CLK
);

  wire and_1_out, and_2_out, and_3_out, and_5_out, and_6_out, and_7_out, and_8_out, and_9_out, and_10_out,
       and_11_out, and_12_out, comparator_1_eq, multiplexer_1_out, multiplexer_5_out, multiplexer_6_out,
       nor_1_out, or_3_out, or_4_out, or_5_out, or_6_out, SEL_q, xnor_1_out, xnor_2_out, xnor_3_out,
       xor_1_out, xor_2_out, xor_3_out, xor_4_out;
  wire [1:0] and_4_out, or_1_out, or_1_out_2, or_2_out, sub_1_c_o;
  wire [2:0] INSTR_d_3;
  wire [3:0] C_q, not_1_out;
  wire [4:0] driver_17_out;
  wire [7:0] and_14_out, and_14_out_2, decoder_1_out_7, decoder_1_out_15, decoder_2_out_7, decoder_2_out_15,
       decoder_3_out_7, decoder_3_out_8, INSTR_d, or_9_out, or_9_out_2;
  wire [11:8] INSTR_d_2;
  wire [15:0] add_1_s, add_2_s, add_3_s, add_4_s, Addr_q, and_13_out, ASR_out, bitextender_1_out,
       bitextender_2_out, BUF_q, div_1_q, div_1_r, driver_1_out, driver_9_out, Link_q, LSL_2_out, LSL_out,
       LSR_out, MEM_d, mul_1_mul, mul_1_mul_2, multiplexer_2_out, multiplexer_3_out, multiplexer_4_out,
       multiplexer_7_out, multiplexer_8_out, multiplexer_9_out, multiplexer_10_out, multiplexer_11_out,
       multiplexer_12_out, multiplexer_13_out, multiplexer_14_out, multiplexer_15_out, multiplexer_16_out,
       multiplexer_17_out, multiplexer_18_out, multiplexer_19_out, multiplexer_20_out, multiplexer_21_out,
       multiplexer_22_out, nor_2_out, or_7_out, or_8_out, PC_out, R1_q, R2_q, R3_q, R4_q, R5_q, R6_q, R7_q,
       R8_q, R9_q, RET_q, ROR_out, STA_q, sub_1_s, xor_5_out;
  wire [15:5] driver_17_out_2;

  ROM #(.bigEndian("true"), .AddrBits(16), .Bits(16)) INSTR (
    .A(PC_out), .sel(1'b1), .D({and_4_out[1], INSTR_d_3, INSTR_d_2, INSTR_d}));
  EEPROMDualPort #(.AddrBits(16), .Bits(16)) MEM (
    .A(driver_9_out), .Din(driver_1_out), .str(and_1_out), .C(CLK), .ld(1'b1), .D(MEM_d));
  assign {or_1_out_2, or_1_out} = INSTR_d[3:0] | INSTR_d[7:4] | INSTR_d_2;  // Or or_1, 4 bits wide
  and and_1 (and_1_out, INSTR_d_3[0], INSTR_d_3[1], ~INSTR_d_3[2], ~and_4_out[1]);  // And
  and and_2 (and_2_out, INSTR_d_3[1], ~INSTR_d_3[2], ~and_4_out[1]);  // And
  and and_3 (and_3_out, INSTR_d_3[1], INSTR_d_3[2]);
  and and_4 (and_4_out[0], INSTR_d_3[0], ~and_4_out[1]);  // And
  and and_5 (and_5_out, INSTR_d_3[0], INSTR_d_3[1], INSTR_d_3[2], and_4_out[1]);
  and and_6 (and_6_out, ~and_4_out[1], INSTR_d_3[2], INSTR_d_3[1], INSTR_d_3[0]);  // And
  assign or_2_out = or_1_out | or_1_out_2;  // Or or_2, 2 bits wide
  or or_3 (or_3_out, and_3_out, and_4_out[1]);
  and and_7 (and_7_out, nor_1_out, and_5_out);
  and and_8 (and_8_out, nor_1_out, and_6_out);
  nor nor_1 (nor_1_out, or_2_out[0], or_2_out[1]);
  or or_4 (or_4_out, C_q[3], C_q[2]);
  or or_5 (or_5_out, ~C_q[3], C_q[2]);  // Or
  xor xor_1 (xor_1_out, C_q[3], C_q[0]);
  and and_9 (and_9_out, ~C_q[2], xnor_1_out);  // And
  or or_6 (or_6_out, C_q[2], ~xnor_1_out);  // Or
  xnor xnor_1 (xnor_1_out, C_q[3], C_q[0]);
  and and_10 (and_10_out, ~C_q[1], ~C_q[0]);  // And
  assign not_1_out = ~C_q;  // Not not_1, 4 bits wide
  Multiplexer #(.Selector_Bits(4)) multiplexer_1 (
    .sel(INSTR_d[3:0]), .in_0(C_q[0]), .in_1(not_1_out[0]), .in_2(C_q[1]), .in_3(not_1_out[1]),
    .in_4(C_q[2]), .in_5(not_1_out[2]), .in_6(C_q[3]), .in_7(not_1_out[3]), .in_8(or_4_out), .in_9(or_5_out),
    .in_10(xor_1_out), .in_11(and_9_out), .in_12(or_6_out), .in_13(xnor_1_out), .in_14(and_10_out),
    .in_15(1'b1), .out(multiplexer_1_out));
  Add #(.Bits(16)) add_1 (.a(driver_1_out), .b(16'h1), .c_i(1'b0), .s(add_1_s));  // open: c_o
  Add #(.Bits(16)) add_2 (.a(driver_1_out), .b(driver_9_out), .c_i(1'b0), .s(add_2_s));  // open: c_o
  BitExtender #(.inputBits(4)) bitextender_1 (.in(INSTR_d[3:0]), .out(bitextender_1_out));
  Multiplexer #(.Bits(16)) multiplexer_2 (
    .sel(multiplexer_1_out), .in_0(add_1_s), .in_1(driver_9_out), .out(multiplexer_2_out));
  Multiplexer #(.Bits(16)) multiplexer_3 (
    .sel(multiplexer_1_out), .in_0(add_1_s), .in_1(add_2_s), .out(multiplexer_3_out));
  Add #(.Bits(16)) add_3 (.a(driver_9_out), .b(bitextender_1_out), .c_i(1'b0), .s(add_3_s));  // open: c_o
  BarrelShifter #(.Bits(16)) LSL (.in(driver_1_out), .shift(5'b01000), .out(LSL_out));
  assign or_7_out = {{8{1'b0}}, INSTR_d} | LSL_out;  // Or or_7, 16 bits wide
  BarrelShifter #(.Bits(16)) LSL_2 (.in(driver_1_out), .shift(driver_17_out), .out(LSL_2_out));
  BarrelShifter #(.Bits(16), .direction("right")) LSR (.in(driver_1_out), .shift(driver_17_out), .out(LSR_out));
  BarrelShifter #(.Bits(16), .barrelShifterMode("arithmetic"), .direction("right")) ASR (
    .in(driver_1_out), .shift(driver_17_out), .out(ASR_out));
  BarrelShifter #(.Bits(16), .barrelShifterMode("rotate"), .direction("right")) ROR (
    .in(driver_1_out), .shift(driver_17_out), .out(ROR_out));
  Multiplexer #(.Selector_Bits(2), .Bits(16)) multiplexer_4 (
    .sel(INSTR_d[5:4]), .in_0(LSL_2_out), .in_1(LSR_out), .in_2(ASR_out), .in_3(ROR_out),
    .out(multiplexer_4_out));
  Comparator #(.Bits(16)) comparator_1 (.a(multiplexer_7_out), .b({16{1'b0}}), .eq(comparator_1_eq));  // open: gt, lt
  xnor xnor_2 (xnor_2_out, driver_9_out[15], driver_17_out_2[15]);
  xor xor_2 (xor_2_out, driver_9_out[15], driver_17_out_2[15]);
  xnor xnor_3 (xnor_3_out, driver_17_out_2[15], multiplexer_7_out[15]);
  xor xor_3 (xor_3_out, xnor_2_out, multiplexer_7_out[15]);
  and and_11 (and_11_out, xor_2_out, xnor_3_out);
  Multiplexer #(.Selector_Bits(2)) multiplexer_5 (
    .sel(and_4_out), .in_0(xor_3_out), .in_1(and_11_out), .in_2(1'b0), .in_3(1'b0), .out(multiplexer_5_out));
  Multiplexer #(.Selector_Bits(2)) multiplexer_6 (
    .sel(and_4_out), .in_0(sub_1_c_o[1]), .in_1(sub_1_c_o[0]), .in_2(1'b0), .in_3(1'b0),
    .out(multiplexer_6_out));
  xor xor_4 (xor_4_out, and_7_out, and_8_out);
  Register SEL (.D(and_7_out), .C(CLK), .en(xor_4_out), .Q(SEL_q));
  and and_12 (and_12_out, SEL_q, or_3_out);
  Register N (.D(multiplexer_7_out[15]), .C(CLK), .en(and_12_out), .Q(C_q[3]));
  Register Z (.D(comparator_1_eq), .C(CLK), .en(and_12_out), .Q(C_q[2]));
  Register C (.D(multiplexer_6_out), .C(CLK), .en(and_12_out), .Q(C_q[1]));
  Register V (.D(multiplexer_5_out), .C(CLK), .en(and_12_out), .Q(C_q[0]));
  Add #(.Bits(16)) add_4 (
    .a(driver_9_out), .b({driver_17_out_2, driver_17_out}), .c_i(C_q[1]), .s(add_4_s), .c_o(sub_1_c_o[1]));
  Sub #(.Bits(16)) sub_1 (
    .a(driver_9_out), .b({driver_17_out_2, driver_17_out}), .c_i(C_q[1]), .s(sub_1_s), .c_o(sub_1_c_o[0]));
  Mul #(.Bits(16)) mul_1 (.a(driver_9_out), .b({driver_17_out_2, driver_17_out}), .mul({mul_1_mul_2, mul_1_mul}));
  Div #(.Bits(16)) div_1 (.a(driver_9_out), .b({driver_17_out_2, driver_17_out}), .q(div_1_q), .r(div_1_r));
  assign and_13_out = driver_9_out & {driver_17_out_2, driver_17_out};  // And and_13, 16 bits wide
  assign or_8_out = driver_9_out | {driver_17_out_2, driver_17_out};  // Or or_8, 16 bits wide
  assign xor_5_out = driver_9_out ^ {driver_17_out_2, driver_17_out};  // XOr xor_5, 16 bits wide
  assign nor_2_out = ~(driver_9_out | {driver_17_out_2, driver_17_out});  // NOr nor_2, 16 bits wide
  BitExtender #(.inputBits(1)) bitextender_2 (.in(and_2_out), .out(bitextender_2_out));
  Multiplexer #(.Selector_Bits(4), .Bits(16)) multiplexer_7 (
    .sel({and_4_out[1], INSTR_d_3}), .in_0(multiplexer_2_out), .in_1(multiplexer_3_out), .in_2(MEM_d),
    .in_3(driver_1_out), .in_4(or_7_out), .in_5(multiplexer_4_out), .in_6(add_4_s), .in_7(sub_1_s),
    .in_8(mul_1_mul), .in_9(mul_1_mul_2), .in_10(div_1_q), .in_11(div_1_r), .in_12(and_13_out),
    .in_13(or_8_out), .in_14(xor_5_out), .in_15(nor_2_out), .out(multiplexer_7_out));
  Decoder #(.Selector_Bits(4)) decoder_1 (
    .sel(INSTR_d[3:0]), .out_0(decoder_1_out_7[0]), .out_1(decoder_1_out_7[1]), .out_2(decoder_1_out_7[2]),
    .out_3(decoder_1_out_7[3]), .out_4(decoder_1_out_7[4]), .out_5(decoder_1_out_7[5]),
    .out_6(decoder_1_out_7[6]), .out_7(decoder_1_out_7[7]), .out_8(decoder_1_out_15[0]),
    .out_9(decoder_1_out_15[1]), .out_10(decoder_1_out_15[2]), .out_11(decoder_1_out_15[3]),
    .out_12(decoder_1_out_15[4]), .out_13(decoder_1_out_15[5]), .out_14(decoder_1_out_15[6]),
    .out_15(decoder_1_out_15[7]));
  Decoder #(.Selector_Bits(4)) decoder_2 (
    .sel(INSTR_d[7:4]), .out_0(decoder_2_out_7[0]), .out_1(decoder_2_out_7[1]), .out_2(decoder_2_out_7[2]),
    .out_3(decoder_2_out_7[3]), .out_4(decoder_2_out_7[4]), .out_5(decoder_2_out_7[5]),
    .out_6(decoder_2_out_7[6]), .out_7(decoder_2_out_7[7]), .out_8(decoder_2_out_15[0]),
    .out_9(decoder_2_out_15[1]), .out_10(decoder_2_out_15[2]), .out_11(decoder_2_out_15[3]),
    .out_12(decoder_2_out_15[4]), .out_13(decoder_2_out_15[5]), .out_14(decoder_2_out_15[6]),
    .out_15(decoder_2_out_15[7]));
  Decoder #(.Selector_Bits(4)) decoder_3 (
    .sel(INSTR_d_2), .out_0(decoder_3_out_7[0]), .out_1(decoder_3_out_7[1]), .out_2(decoder_3_out_7[2]),
    .out_3(decoder_3_out_7[3]), .out_4(decoder_3_out_7[4]), .out_5(decoder_3_out_7[5]),
    .out_6(decoder_3_out_7[6]), .out_7(decoder_3_out_7[7]), .out_8(decoder_3_out_8[0]),
    .out_9(decoder_3_out_8[1]), .out_10(decoder_3_out_8[2]), .out_11(decoder_3_out_8[3]),
    .out_12(decoder_3_out_8[4]), .out_13(decoder_3_out_8[5]), .out_14(decoder_3_out_8[6]),
    .out_15(decoder_3_out_8[7]));
  assign {or_9_out_2, or_9_out} = {and_14_out_2, and_14_out} | {decoder_3_out_8, decoder_3_out_7};  // Or or_9, 16 bits wide
  assign {and_14_out_2, and_14_out} = bitextender_2_out & {decoder_2_out_15, decoder_2_out_7};  // And and_14, 16 bits wide
  Multiplexer #(.Bits(16)) multiplexer_8 (
    .sel(and_14_out[1]), .in_0(multiplexer_7_out), .in_1(add_3_s), .out(multiplexer_8_out));
  Multiplexer #(.Bits(16)) multiplexer_9 (
    .sel(and_14_out[2]), .in_0(multiplexer_7_out), .in_1(add_3_s), .out(multiplexer_9_out));
  Multiplexer #(.Bits(16)) multiplexer_10 (
    .sel(and_14_out[3]), .in_0(multiplexer_7_out), .in_1(add_3_s), .out(multiplexer_10_out));
  Multiplexer #(.Bits(16)) multiplexer_11 (
    .sel(and_14_out[4]), .in_0(multiplexer_7_out), .in_1(add_3_s), .out(multiplexer_11_out));
  Multiplexer #(.Bits(16)) multiplexer_12 (
    .sel(and_14_out[5]), .in_0(multiplexer_7_out), .in_1(add_3_s), .out(multiplexer_12_out));
  Multiplexer #(.Bits(16)) multiplexer_13 (
    .sel(and_14_out[6]), .in_0(multiplexer_7_out), .in_1(add_3_s), .out(multiplexer_13_out));
  Multiplexer #(.Bits(16)) multiplexer_14 (
    .sel(and_14_out[7]), .in_0(multiplexer_7_out), .in_1(add_3_s), .out(multiplexer_14_out));
  Register #(.Bits(16)) R1 (.D(multiplexer_8_out), .C(CLK), .en(or_9_out[1]), .Q(R1_q));
  Register #(.Bits(16)) R2 (.D(multiplexer_9_out), .C(CLK), .en(or_9_out[2]), .Q(R2_q));
  Register #(.Bits(16)) R3 (.D(multiplexer_10_out), .C(CLK), .en(or_9_out[3]), .Q(R3_q));
  Register #(.Bits(16)) R4 (.D(multiplexer_11_out), .C(CLK), .en(or_9_out[4]), .Q(R4_q));
  Register #(.Bits(16)) R5 (.D(multiplexer_12_out), .C(CLK), .en(or_9_out[5]), .Q(R5_q));
  Register #(.Bits(16)) R6 (.D(multiplexer_13_out), .C(CLK), .en(or_9_out[6]), .Q(R6_q));
  Register #(.Bits(16)) R7 (.D(multiplexer_14_out), .C(CLK), .en(or_9_out[7]), .Q(R7_q));
  assign driver_1_out = decoder_3_out_7[0] ? {16{1'b0}} : 16'bz;  // Driver driver_1
  assign driver_1_out = decoder_3_out_7[1] ? R1_q : 16'bz;  // Driver driver_2
  assign driver_1_out = decoder_3_out_7[2] ? R2_q : 16'bz;  // Driver driver_3
  assign driver_1_out = decoder_3_out_7[3] ? R3_q : 16'bz;  // Driver driver_4
  assign driver_1_out = decoder_3_out_7[4] ? R4_q : 16'bz;  // Driver driver_5
  assign driver_1_out = decoder_3_out_7[5] ? R5_q : 16'bz;  // Driver driver_6
  assign driver_1_out = decoder_3_out_7[6] ? R6_q : 16'bz;  // Driver driver_7
  assign driver_1_out = decoder_3_out_7[7] ? R7_q : 16'bz;  // Driver driver_8
  assign driver_9_out = decoder_2_out_7[0] ? {16{1'b0}} : 16'bz;  // Driver driver_9
  assign driver_9_out = decoder_2_out_7[1] ? R1_q : 16'bz;  // Driver driver_10
  assign driver_9_out = decoder_2_out_7[2] ? R2_q : 16'bz;  // Driver driver_11
  assign driver_9_out = decoder_2_out_7[3] ? R3_q : 16'bz;  // Driver driver_12
  assign driver_9_out = decoder_2_out_7[4] ? R4_q : 16'bz;  // Driver driver_13
  assign driver_9_out = decoder_2_out_7[5] ? R5_q : 16'bz;  // Driver driver_14
  assign driver_9_out = decoder_2_out_7[6] ? R6_q : 16'bz;  // Driver driver_15
  assign driver_9_out = decoder_2_out_7[7] ? R7_q : 16'bz;  // Driver driver_16
  assign {driver_17_out_2, driver_17_out} = decoder_1_out_7[0] ? {16{1'b0}} : 16'bz;  // Driver driver_17
  // Probe on R1_q
  assign {driver_17_out_2, driver_17_out} = decoder_1_out_7[1] ? R1_q : 16'bz;  // Driver driver_18
  // Probe on R2_q
  assign {driver_17_out_2, driver_17_out} = decoder_1_out_7[2] ? R2_q : 16'bz;  // Driver driver_19
  // Probe on R3_q
  assign {driver_17_out_2, driver_17_out} = decoder_1_out_7[3] ? R3_q : 16'bz;  // Driver driver_20
  // Probe on R4_q
  assign {driver_17_out_2, driver_17_out} = decoder_1_out_7[4] ? R4_q : 16'bz;  // Driver driver_21
  // Probe on R5_q
  assign {driver_17_out_2, driver_17_out} = decoder_1_out_7[5] ? R5_q : 16'bz;  // Driver driver_22
  // Probe on R6_q
  assign {driver_17_out_2, driver_17_out} = decoder_1_out_7[6] ? R6_q : 16'bz;  // Driver driver_23
  // Probe on R7_q
  assign {driver_17_out_2, driver_17_out} = decoder_1_out_7[7] ? R7_q : 16'bz;  // Driver driver_24
  Multiplexer #(.Bits(16)) multiplexer_15 (
    .sel(and_14_out_2[0]), .in_0(multiplexer_7_out), .in_1(add_3_s), .out(multiplexer_15_out));
  Multiplexer #(.Bits(16)) multiplexer_16 (
    .sel(and_14_out_2[1]), .in_0(multiplexer_7_out), .in_1(add_3_s), .out(multiplexer_16_out));
  Multiplexer #(.Bits(16)) multiplexer_17 (
    .sel(and_14_out_2[2]), .in_0(multiplexer_7_out), .in_1(add_3_s), .out(multiplexer_17_out));
  Multiplexer #(.Bits(16)) multiplexer_18 (
    .sel(and_14_out_2[3]), .in_0(multiplexer_7_out), .in_1(add_3_s), .out(multiplexer_18_out));
  Multiplexer #(.Bits(16)) multiplexer_19 (
    .sel(and_14_out_2[4]), .in_0(multiplexer_7_out), .in_1(add_3_s), .out(multiplexer_19_out));
  Multiplexer #(.Bits(16)) multiplexer_20 (
    .sel(and_14_out_2[5]), .in_0(multiplexer_7_out), .in_1(add_3_s), .out(multiplexer_20_out));
  Multiplexer #(.Bits(16)) multiplexer_21 (
    .sel(and_14_out_2[6]), .in_0(multiplexer_7_out), .in_1(add_3_s), .out(multiplexer_21_out));
  Multiplexer #(.Bits(16)) multiplexer_22 (
    .sel(and_14_out_2[7]), .in_0(multiplexer_7_out), .in_1(add_3_s), .out(multiplexer_22_out));
  Register #(.Bits(16)) R8 (.D(multiplexer_15_out), .C(CLK), .en(or_9_out_2[0]), .Q(R8_q));
  Register #(.Bits(16)) R9 (.D(multiplexer_16_out), .C(CLK), .en(or_9_out_2[1]), .Q(R9_q));
  Register #(.Bits(16)) BUF (.D(multiplexer_17_out), .C(CLK), .en(or_9_out_2[2]), .Q(BUF_q));
  Register #(.Bits(16)) RET (.D(multiplexer_18_out), .C(CLK), .en(or_9_out_2[3]), .Q(RET_q));
  Register #(.Bits(16)) STA (.D(multiplexer_19_out), .C(CLK), .en(or_9_out_2[4]), .Q(STA_q));
  Register #(.Bits(16)) Addr (.D(multiplexer_20_out), .C(CLK), .en(or_9_out_2[5]), .Q(Addr_q));
  Register #(.Bits(16)) Link (.D(multiplexer_21_out), .C(CLK), .en(or_9_out_2[6]), .Q(Link_q));
  CounterPreset #(.Bits(16)) PC (
    .en(1'b1), .C(CLK), .dir(1'b0), .in(multiplexer_22_out), .ld(or_9_out_2[7]), .clr(1'b0), .out(PC_out));  // open: ovf
  assign driver_1_out = decoder_3_out_8[0] ? R8_q : 16'bz;  // Driver driver_25
  assign driver_1_out = decoder_3_out_8[1] ? R9_q : 16'bz;  // Driver driver_26
  assign driver_1_out = decoder_3_out_8[2] ? BUF_q : 16'bz;  // Driver driver_27
  assign driver_1_out = decoder_3_out_8[3] ? RET_q : 16'bz;  // Driver driver_28
  assign driver_1_out = decoder_3_out_8[4] ? STA_q : 16'bz;  // Driver driver_29
  assign driver_1_out = decoder_3_out_8[5] ? Addr_q : 16'bz;  // Driver driver_30
  assign driver_1_out = decoder_3_out_8[6] ? Link_q : 16'bz;  // Driver driver_31
  assign driver_1_out = decoder_3_out_8[7] ? PC_out : 16'bz;  // Driver driver_32
  assign driver_9_out = decoder_2_out_15[0] ? R8_q : 16'bz;  // Driver driver_33
  assign driver_9_out = decoder_2_out_15[1] ? R9_q : 16'bz;  // Driver driver_34
  assign driver_9_out = decoder_2_out_15[2] ? BUF_q : 16'bz;  // Driver driver_35
  assign driver_9_out = decoder_2_out_15[3] ? RET_q : 16'bz;  // Driver driver_36
  assign driver_9_out = decoder_2_out_15[4] ? STA_q : 16'bz;  // Driver driver_37
  assign driver_9_out = decoder_2_out_15[5] ? Addr_q : 16'bz;  // Driver driver_38
  assign driver_9_out = decoder_2_out_15[6] ? Link_q : 16'bz;  // Driver driver_39
  assign driver_9_out = decoder_2_out_15[7] ? PC_out : 16'bz;  // Driver driver_40
  assign {driver_17_out_2, driver_17_out} = decoder_1_out_15[0] ? R8_q : 16'bz;  // Driver driver_41
  assign {driver_17_out_2, driver_17_out} = decoder_1_out_15[1] ? R9_q : 16'bz;  // Driver driver_42
  assign {driver_17_out_2, driver_17_out} = decoder_1_out_15[2] ? BUF_q : 16'bz;  // Driver driver_43
  assign {driver_17_out_2, driver_17_out} = decoder_1_out_15[3] ? RET_q : 16'bz;  // Driver driver_44
  assign {driver_17_out_2, driver_17_out} = decoder_1_out_15[4] ? STA_q : 16'bz;  // Driver driver_45
  assign {driver_17_out_2, driver_17_out} = decoder_1_out_15[5] ? Addr_q : 16'bz;  // Driver driver_46
  assign {driver_17_out_2, driver_17_out} = decoder_1_out_15[6] ? Link_q : 16'bz;  // Driver driver_47
  assign {driver_17_out_2, driver_17_out} = decoder_1_out_15[7] ? PC_out : 16'bz;  // Driver driver_48
  // Probe on R8_q
  // Probe on R9_q
  // Probe on BUF_q
  // Probe on RET_q
  // Probe on STA_q
  // Probe on Addr_q
  // Probe on Link_q
  // Probe on PC_out

  // Notes on the sheet:
  //   CLK: Hz: 10
  //   INSTR loads fibbo.asm.hex
  //   contents of MEM (hex, n*v repeats v):
  //   b520
  //   CONTROL UNIT
  //   OPERAND
  //   OPCODE
  //   NOR
  //   XOR
  //   CLK
  //   Rm
  //   Rn
  //   Rd
  //   IMM8
  //   OPRAND
  //   LDR
  //   MemWE
  //   RnWE
  //   NZCV EN
  //   CV SEL
  //   NZCV ON
  //   NZCV RST
  //   CONDITIONS
  //   N
  //   Z
  //   C
  //   V
  //   NS
  //   NC
  //   ZS
  //   ZC
  //   CS
  //   CC
  //   VS
  //   VC
  //   SM
  //   HI
  //   LT
  //   GT
  //   LE
  //   GE
  //   FC
  //   AL
  //   OP
  //   CND
  //   Dd
  //   Dn
  //   PC
  //   BRANCH
  //   POST IDX
  //   MVS
  //   SHIFT
  //   DnIN
  //   Dm
  //   MOV
  //   CNS
  //   SFT
  //   CARRY
  //   NZCV CONTROL UNIT
  //   DdIN
  //   NZCV SELECT BIT
  //   NZCV REGISTERS
  //   ALU
  //   REGISTER FILE
  //   STR
  //   ADD
  //   SUB
  //   MUL
  //   LML
  //   DIV
  //   MOD
  //   AND
  //   ORR
  //   WE
  //   Didx
  //   Zero
  //   Buffer Register
  //   Return Register
  //   Stack Pointer
  //   Address Register
  //   Link Register
  //   Program Counter
endmodule
